// Logisim project RISC_V_CPU_32.circ as structural Verilog
module ALU (
  input  [31:0] A,
  input  [31:0] B,
  input  [3:0] ALUControl,
  output [31:0] Result
);

  wire comparator_1_lt, comparator_2_lt;
  wire [31:0] adder_1_out, and_1_out, multiplexer_1_out, multiplexer_2_out, or_1_out, shifter_1_out,
       shifter_2_out, shifter_3_out, subtractor_1_out, xor_1_out;

  Adder #(.width(32)) adder_1 (.a(A), .b(B), .out(adder_1_out), .cin(1'b0));  // open: cout
  Subtractor #(.width(32)) subtractor_1 (.a(A), .b(B), .out(subtractor_1_out), .bin(1'b0));  // open: bout
  assign and_1_out = A & B;  // AND_Gate and_1, 32 bits wide
  assign or_1_out = A | B;  // OR_Gate or_1, 32 bits wide
  assign xor_1_out = A ^ B;  // XOR_Gate xor_1, 32 bits wide
  Comparator #(.width(32)) comparator_1 (.a(A), .b(B), .lt(comparator_1_lt));  // open: gt, eq
  Comparator #(.mode("unsigned"), .width(32)) comparator_2 (.a(A), .b(B), .lt(comparator_2_lt));  // open: gt, eq
  Shifter #(.width(32)) shifter_1 (.in(A), .\dist (B[4:0]), .out(shifter_1_out));
  Shifter #(.shift("lr"), .width(32)) shifter_2 (.in(A), .\dist (B[4:0]), .out(shifter_2_out));
  Shifter #(.shift("ar"), .width(32)) shifter_3 (.in(A), .\dist (B[4:0]), .out(shifter_3_out));
  Multiplexer #(.width(32)) multiplexer_1 (
    .in0({32{1'b0}}), .in1(32'h1), .out(multiplexer_1_out), .sel(comparator_1_lt));
  Multiplexer #(.width(32)) multiplexer_2 (
    .in0({32{1'b0}}), .in1(32'h1), .out(multiplexer_2_out), .sel(comparator_2_lt));
  Multiplexer #(.select(4), .width(32)) multiplexer_3 (
    .in0(adder_1_out), .in1(subtractor_1_out), .in2(and_1_out), .in3(or_1_out), .in4(xor_1_out),
    .in5(multiplexer_1_out), .in6(multiplexer_2_out), .in7(shifter_1_out), .in8(shifter_2_out),
    .in9(shifter_3_out), .in10({32{1'b0}}), .in11({32{1'b0}}), .in12({32{1'b0}}), .in13({32{1'b0}}),
    .in14({32{1'b0}}), .in15({32{1'b0}}), .out(Result), .sel(ALUControl));

  // Notes on the sheet:
  //   ALUControl: initial=0x9
  //   B: initial=0x2
endmodule

module RegisterFile (
  input  [4:0] ReadReg1,
  input  [4:0] ReadReg2,
  input  [4:0] WriteReg,
  input  RegWrite,
  input  [31:0] WriteData,
  input  Clock,
  output [31:0] ReadData1,
  output [31:0] ReadData2
);

  wire WE1, WE2, WE3, WE4, WE5, WE6, WE7, WE8, WE9, WE10, WE11, WE12, WE13, WE14, WE15, WE16, WE17, WE18,
       WE19, WE20, WE21, WE22, WE23, WE24, WE25, WE26, WE27, WE28, WE29, WE30, WE31;
  wire [31:0] R1, R2, R3, R4, R5, R6, R7, R8, R9, R10, R11, R12, R13, R14, R15, R16, R17, R18, R19, R20, R21,
       R22, R23, R24, R25, R26, R27, R28, R29, R30, R31;

  Decoder #(.select(5)) decoder_1 (
    .out1(WE1), .out2(WE2), .out3(WE3), .out4(WE4), .out5(WE5), .out6(WE6), .out7(WE7), .out8(WE8),
    .out9(WE9), .out10(WE10), .out11(WE11), .out12(WE12), .out13(WE13), .out14(WE14), .out15(WE15),
    .out16(WE16), .out17(WE17), .out18(WE18), .out19(WE19), .out20(WE20), .out21(WE21), .out22(WE22),
    .out23(WE23), .out24(WE24), .out25(WE25), .out26(WE26), .out27(WE27), .out28(WE28), .out29(WE29),
    .out30(WE30), .out31(WE31), .sel(WriteReg), .en(RegWrite));  // open: out0
  Register #(.width(32)) register_1 (.D(WriteData), .en(WE1), .clk(Clock), .Q(R1));  // open: clr
  Register #(.width(32)) register_2 (.D(WriteData), .en(WE2), .clk(Clock), .Q(R2));  // open: clr
  Register #(.width(32)) register_3 (.D(WriteData), .en(WE3), .clk(Clock), .Q(R3));  // open: clr
  Register #(.width(32)) register_4 (.D(WriteData), .en(WE4), .clk(Clock), .Q(R4));  // open: clr
  Register #(.width(32)) register_5 (.D(WriteData), .en(WE5), .clk(Clock), .Q(R5));  // open: clr
  Register #(.width(32)) register_6 (.D(WriteData), .en(WE6), .clk(Clock), .Q(R6));  // open: clr
  Register #(.width(32)) register_7 (.D(WriteData), .en(WE7), .clk(Clock), .Q(R7));  // open: clr
  Register #(.width(32)) register_8 (.D(WriteData), .en(WE8), .clk(Clock), .Q(R8));  // open: clr
  Register #(.width(32)) register_9 (.D(WriteData), .en(WE9), .clk(Clock), .Q(R9));  // open: clr
  Register #(.width(32)) register_10 (.D(WriteData), .en(WE10), .clk(Clock), .Q(R10));  // open: clr
  Register #(.width(32)) register_11 (.D(WriteData), .en(WE11), .clk(Clock), .Q(R11));  // open: clr
  Register #(.width(32)) register_12 (.D(WriteData), .en(WE12), .clk(Clock), .Q(R12));  // open: clr
  Register #(.width(32)) register_13 (.D(WriteData), .en(WE13), .clk(Clock), .Q(R13));  // open: clr
  Register #(.width(32)) register_14 (.D(WriteData), .en(WE14), .clk(Clock), .Q(R14));  // open: clr
  Register #(.width(32)) register_15 (.D(WriteData), .en(WE15), .clk(Clock), .Q(R15));  // open: clr
  Register #(.width(32)) register_16 (.D(WriteData), .en(WE16), .clk(Clock), .Q(R16));  // open: clr
  Register #(.width(32)) register_17 (.D(WriteData), .en(WE17), .clk(Clock), .Q(R17));  // open: clr
  Register #(.width(32)) register_18 (.D(WriteData), .en(WE18), .clk(Clock), .Q(R18));  // open: clr
  Register #(.width(32)) register_19 (.D(WriteData), .en(WE19), .clk(Clock), .Q(R19));  // open: clr
  Register #(.width(32)) register_20 (.D(WriteData), .en(WE20), .clk(Clock), .Q(R20));  // open: clr
  Register #(.width(32)) register_21 (.D(WriteData), .en(WE21), .clk(Clock), .Q(R21));  // open: clr
  Register #(.width(32)) register_22 (.D(WriteData), .en(WE22), .clk(Clock), .Q(R22));  // open: clr
  Register #(.width(32)) register_23 (.D(WriteData), .en(WE23), .clk(Clock), .Q(R23));  // open: clr
  Register #(.width(32)) register_24 (.D(WriteData), .en(WE24), .clk(Clock), .Q(R24));  // open: clr
  Register #(.width(32)) register_25 (.D(WriteData), .en(WE25), .clk(Clock), .Q(R25));  // open: clr
  Register #(.width(32)) register_26 (.D(WriteData), .en(WE26), .clk(Clock), .Q(R26));  // open: clr
  Register #(.width(32)) register_27 (.D(WriteData), .en(WE27), .clk(Clock), .Q(R27));  // open: clr
  Register #(.width(32)) register_28 (.D(WriteData), .en(WE28), .clk(Clock), .Q(R28));  // open: clr
  Register #(.width(32)) register_29 (.D(WriteData), .en(WE29), .clk(Clock), .Q(R29));  // open: clr
  Register #(.width(32)) register_30 (.D(WriteData), .en(WE30), .clk(Clock), .Q(R30));  // open: clr
  Register #(.width(32)) register_31 (.D(WriteData), .en(WE31), .clk(Clock), .Q(R31));  // open: clr
  Multiplexer #(.select(5), .width(32)) multiplexer_1 (
    .in0({32{1'b0}}), .in1(R1), .in2(R2), .in3(R3), .in4(R4), .in5(R5), .in6(R6), .in7(R7), .in8(R8),
    .in9(R9), .in10(R10), .in11(R11), .in12(R12), .in13(R13), .in14(R14), .in15(R15), .in16(R16), .in17(R17),
    .in18(R18), .in19(R19), .in20(R20), .in21(R21), .in22(R22), .in23(R23), .in24(R24), .in25(R25),
    .in26(R26), .in27(R27), .in28(R28), .in29(R29), .in30(R30), .in31(R31), .out(ReadData1), .sel(ReadReg1));
  Multiplexer #(.select(5), .width(32)) multiplexer_2 (
    .in0({32{1'b0}}), .in1(R1), .in2(R2), .in3(R3), .in4(R4), .in5(R5), .in6(R6), .in7(R7), .in8(R8),
    .in9(R9), .in10(R10), .in11(R11), .in12(R12), .in13(R13), .in14(R14), .in15(R15), .in16(R16), .in17(R17),
    .in18(R18), .in19(R19), .in20(R20), .in21(R21), .in22(R22), .in23(R23), .in24(R24), .in25(R25),
    .in26(R26), .in27(R27), .in28(R28), .in29(R29), .in30(R30), .in31(R31), .out(ReadData2), .sel(ReadReg2));

  // Other names for the same wires on the sheet: OUT1[31:0] = ReadData1; OUT2[31:0] = ReadData2; SEL1[4:0] = ReadReg1;
  //   SEL2[4:0] = ReadReg2

  // Notes on the sheet:
  //   RegWrite: initial=0x1
  //   WriteData: initial=0x7b
  //   WriteReg: initial=0x1
endmodule

module ImmediateGenerator (
  input  [31:0] Instruction,
  input  [2:0] ImmType,
  output [31:0] Immediate,
  output [31:0] Imm_S,
  output [31:0] Imm_I,
  output [31:0] Imm_B,
  output [31:0] Imm_U,
  output [31:0] Imm_J
);

  assign Imm_I = {{20{Instruction[31]}}, Instruction[31:20]};  // Bit_Extender bit_extender_1
  Multiplexer #(.select(3), .width(32)) multiplexer_1 (
    .in0(Imm_I), .in1(Imm_S), .in2(Imm_B), .in3({Instruction[31:12], {12{1'b0}}}), .in4(Imm_J),
    .in5({32{1'b0}}), .in6({32{1'b0}}), .in7({32{1'b0}}), .out(Immediate), .sel(ImmType));
  assign Imm_S = {{20{Instruction[31]}}, {Instruction[31:25], Instruction[11:7]}};  // Bit_Extender bit_extender_2
  assign Imm_B = {{19{Instruction[31]}}, {Instruction[31], Instruction[7], Instruction[30:25], Instruction[11:8], 1'b0}};  // Bit_Extender bit_extender_3
  assign Imm_J = {{11{Instruction[31]}}, {Instruction[31], Instruction[19:12], Instruction[20], Instruction[30:21], 1'b0}};  // Bit_Extender bit_extender_4

  assign Imm_U = {Instruction[31:12], {12{1'b0}}};

  // Notes on the sheet:
  //   Instruction: initial=0xef
  //   ImmType: initial=0x4
endmodule

module ControlUnit (
  input  [6:0] Opcode,
  input  [2:0] Funct3,
  input  [6:0] Funct7,
  output [2:0] ImmType,
  output [3:0] ALUControl,
  output ALUSrc,
  output RegWrite,
  output MemRead,
  output MemWrite,
  output [1:0] ResultSrc,
  output Branch,
  output Jump,
  output BranchType
);

  wire ac0_a, ac0_b, ac0_c, ac1_a, ac2_a, ac2_b, add_addr, as_ab, f3_000, f3_001, f3_010, f3_011, f3_100,
       f3_101, f3_110, f3_111, f7_0, f7_20, I_f7_0, I_f7_20, isAUIPC, isBEQ, isBranchOpcode, isIType, isJALR,
       isLUI, isRType, isUImm, load_or_store, opADD, opADD_aux, opADD_I, opADD_R, opADD_RI, opAND, opAND_I,
       opAND_R, opOR, opOR_I, opOR_R, opSLL, opSLL_I, opSLL_R, opSLT, opSLT_I, opSLT_R, opSLTU, opSLTU_I,
       opSLTU_R, opSRA, opSRA_I, opSRA_R, opSRL, opSRL_I, opSRL_R, opSUB, opSUB_R, opXOR, opXOR_I, opXOR_R,
       R_f7_0, R_f7_20, rw_a, rw_a1, rw_ab;

  Comparator #(.width(7)) comparator_1 (.a(Opcode), .b(7'b0110011), .eq(isRType));  // open: gt, lt
  Comparator #(.width(7)) comparator_2 (.a(Opcode), .b(7'b0010011), .eq(isIType));  // open: gt, lt
  Comparator #(.width(7)) comparator_3 (.a(Opcode), .b(7'b0000011), .eq(MemRead));  // open: gt, lt
  Comparator #(.width(7)) comparator_4 (.a(Opcode), .b(7'b0100011), .eq(MemWrite));  // open: gt, lt
  Comparator #(.width(7)) comparator_5 (.a(Opcode), .b(7'b1100011), .eq(isBranchOpcode));  // open: gt, lt
  Comparator #(.width(7)) comparator_6 (.a(Opcode), .b(7'b0110111), .eq(isLUI));  // open: gt, lt
  Comparator #(.width(7)) comparator_7 (.a(Opcode), .b(7'b0010111), .eq(isAUIPC));  // open: gt, lt
  Comparator #(.width(7)) comparator_8 (.a(Opcode), .b(7'b1101111), .eq(ImmType[2]));  // open: gt, lt
  Comparator #(.width(7)) comparator_9 (.a(Opcode), .b(7'b1100111), .eq(isJALR));  // open: gt, lt
  Comparator #(.width(3)) comparator_10 (.a(Funct3), .b(3'b000), .eq(f3_000));  // open: gt, lt
  Comparator #(.width(3)) comparator_11 (.a(Funct3), .b(3'b001), .eq(f3_001));  // open: gt, lt
  Comparator #(.width(3)) comparator_12 (.a(Funct3), .b(3'b010), .eq(f3_010));  // open: gt, lt
  Comparator #(.width(3)) comparator_13 (.a(Funct3), .b(3'b011), .eq(f3_011));  // open: gt, lt
  Comparator #(.width(3)) comparator_14 (.a(Funct3), .b(3'b100), .eq(f3_100));  // open: gt, lt
  Comparator #(.width(3)) comparator_15 (.a(Funct3), .b(3'b101), .eq(f3_101));  // open: gt, lt
  Comparator #(.width(3)) comparator_16 (.a(Funct3), .b(3'b110), .eq(f3_110));  // open: gt, lt
  Comparator #(.width(3)) comparator_17 (.a(Funct3), .b(3'b111), .eq(f3_111));  // open: gt, lt
  Comparator #(.width(7)) comparator_18 (.a(Funct7), .b({7{1'b0}}), .eq(f7_0));  // open: gt, lt
  Comparator #(.width(7)) comparator_19 (.a(Funct7), .b(7'b0100000), .eq(f7_20));  // open: gt, lt
  and and_1 (R_f7_0, isRType, f7_0);
  and and_2 (R_f7_20, isRType, f7_20);
  and and_3 (I_f7_0, isIType, f7_0);
  and and_4 (I_f7_20, isIType, f7_20);
  and and_5 (opADD_R, R_f7_0, f3_000);
  and and_6 (opSUB_R, R_f7_20, f3_000);
  and and_7 (opAND_R, R_f7_0, f3_111);
  and and_8 (opOR_R, R_f7_0, f3_110);
  and and_9 (opXOR_R, R_f7_0, f3_100);
  and and_10 (opSLT_R, R_f7_0, f3_010);
  and and_11 (opSLTU_R, R_f7_0, f3_011);
  and and_12 (opSLL_R, R_f7_0, f3_001);
  and and_13 (opSRL_R, R_f7_0, f3_101);
  and and_14 (opSRA_R, R_f7_20, f3_101);
  and and_15 (opADD_I, isIType, f3_000);
  and and_16 (opAND_I, isIType, f3_111);
  and and_17 (opOR_I, isIType, f3_110);
  and and_18 (opXOR_I, isIType, f3_100);
  and and_19 (opSLT_I, isIType, f3_010);
  and and_20 (opSLTU_I, isIType, f3_011);
  and and_21 (opSLL_I, I_f7_0, f3_001);
  and and_22 (opSRL_I, I_f7_0, f3_101);
  and and_23 (opSRA_I, I_f7_20, f3_101);
  or or_1 (load_or_store, MemRead, MemWrite);
  or or_2 (add_addr, load_or_store, isJALR);
  or or_3 (isUImm, isLUI, isAUIPC);
  and and_24 (isBEQ, isBranchOpcode, f3_000);
  and and_25 (BranchType, isBranchOpcode, f3_001);
  or or_4 (Branch, isBEQ, BranchType);
  or or_5 (opADD_RI, opADD_R, opADD_I);
  or or_6 (opADD_aux, add_addr, isUImm);
  or or_7 (opADD, opADD_RI, opADD_aux);
  or or_8 (opSUB, opSUB_R, Branch);
  or or_9 (opAND, opAND_R, opAND_I);
  or or_10 (opOR, opOR_R, opOR_I);
  or or_11 (opXOR, opXOR_R, opXOR_I);
  or or_12 (opSLT, opSLT_R, opSLT_I);
  or or_13 (opSLTU, opSLTU_R, opSLTU_I);
  or or_14 (opSLL, opSLL_R, opSLL_I);
  or or_15 (opSRL, opSRL_R, opSRL_I);
  or or_16 (opSRA, opSRA_R, opSRA_I);
  or or_17 (ALUControl[3], opSRL, opSRA);
  or or_18 (ac2_a, opXOR, opSLT);
  or or_19 (ac2_b, opSLTU, opSLL);
  or or_20 (ALUControl[2], ac2_a, ac2_b);
  or or_21 (ac1_a, opAND, opOR);
  or or_22 (ALUControl[1], ac1_a, ac2_b);
  or or_23 (ac0_a, opSUB, opOR);
  or or_24 (ac0_b, opSLT, opSLL);
  or or_25 (ac0_c, ac0_a, ac0_b);
  or or_26 (ALUControl[0], ac0_c, opSRA);
  or or_27 (ImmType[1], isBranchOpcode, isUImm);
  or or_28 (ImmType[0], MemWrite, isUImm);
  or or_29 (rw_a1, isRType, isIType);
  or or_30 (rw_a, rw_a1, MemRead);
  or or_31 (Jump, ImmType[2], isJALR);
  or or_32 (rw_ab, rw_a, isUImm);
  or or_33 (RegWrite, rw_ab, Jump);
  or or_34 (as_ab, isIType, add_addr);
  or or_35 (ALUSrc, as_ab, isUImm);

  assign ResultSrc = {Jump, MemRead};

  // Other names for the same wires on the sheet: ALUCtrl0 = ALUControl[0]; ALUCtrl1 = ALUControl[1];
  //   ALUCtrl2 = ALUControl[2]; ALUCtrl3 = ALUControl[3]; isJAL = ImmType[2]; isBNE = BranchType; isStore = MemWrite;
  //   isLoad = MemRead; isJump = Jump; sig_ALUSrc = ALUSrc; sig_Branch = Branch; sig_RegWrite = RegWrite

  // Notes on the sheet:
  //   Opcode: initial=0x63
endmodule

module InstructionMemory (
  input  [31:0] Address,
  output [31:0] Instruction
);

  ROM #(.addrWidth(4), .dataWidth(32)) rom_1 (.addr(Address[5:2]), .data(Instruction));

  // Notes on the sheet:
  //   contents of rom_1 (hex, n*v repeats v):
  //   2000293 8000ef 6300113 108193 2000313 303e7 6300213 6200213 138413 7*13
endmodule

module DataMemory (
  input  [31:0] Address,
  input  [31:0] WriteData,
  input  MemWrite,
  input  Clock,
  input  MemRead,
  output [31:0] ReadData
);

  wire [31:0] ram_1_dout;

  RAM #(.addrWidth(4), .asyncread("true"), .dataWidth(32)) ram_1 (
    .addr(Address[5:2]), .we(MemWrite), .oe(1'b1), .clk(Clock), .din(WriteData), .dout(ram_1_dout));
  Multiplexer #(.width(32)) multiplexer_1 (.in0({32{1'b0}}), .in1(ram_1_dout), .out(ReadData), .sel(MemRead));
endmodule

module PC (
  input  [31:0] PCNext,
  input  Reset,
  input  Clock,
  output [31:0] PCOut
);

  wire [31:0] multiplexer_1_out;

  Multiplexer #(.width(32)) multiplexer_1 (.in0(PCNext), .in1({32{1'b0}}), .out(multiplexer_1_out), .sel(Reset));
  Register #(.width(32)) register_1 (.D(multiplexer_1_out), .clk(Clock), .Q(PCOut));  // open: en, clr

  // Notes on the sheet:
  //   Clock: initial=0x8
endmodule

module SingleCycleCPU (
  input  Clock,
  input  Reset,
  output [31:0] DebugPC,
  output [31:0] DebugInstruction,
  output [31:0] DebugALUResult
);

  wire ALUSrc, beq_cond, bne_cond, Branch, branch_cond, BranchTaken, BranchType, Equal, isAUIPC, isBEQ_type,
       isJAL, isJALR, isLUI, Jump, MemRead, MemWrite, NotEqual, RegWrite, selJAL, selJALR;
  wire [1:0] ResultSrc;
  wire [2:0] ImmType;
  wire [3:0] ALUControl;
  wire [31:0] adder_3_out, ALUA, ALUB, Imm32, MemReadData, multiplexer_1_out, multiplexer_3_out,
       multiplexer_4_out, multiplexer_7_out, PCImmTarget, PCJALR, PCNext, PCPlus4, RegA, RegB, WriteBackData;

  Comparator #(.width(7)) comparator_1 (.a(DebugInstruction[6:0]), .b(7'b0110111), .eq(isLUI));  // open: gt, lt
  Comparator #(.width(7)) comparator_2 (.a(DebugInstruction[6:0]), .b(7'b0010111), .eq(isAUIPC));  // open: gt, lt
  Comparator #(.width(7)) comparator_3 (.a(DebugInstruction[6:0]), .b(7'b1101111), .eq(isJAL));  // open: gt, lt
  Comparator #(.width(7)) comparator_4 (.a(DebugInstruction[6:0]), .b(7'b1100111), .eq(isJALR));  // open: gt, lt
  PC pc_1 (.PCNext(PCNext), .Reset(Reset), .Clock(Clock), .PCOut(DebugPC));
  Multiplexer #(.width(32)) multiplexer_1 (.in0(PCPlus4), .in1(PCImmTarget), .out(multiplexer_1_out), .sel(selJAL));
  InstructionMemory instructionmemory_1 (.Address(DebugPC), .Instruction(DebugInstruction));
  ControlUnit controlunit_1 (
    .Opcode(DebugInstruction[6:0]), .Funct3(DebugInstruction[14:12]), .Funct7(DebugInstruction[31:25]),
    .ImmType(ImmType), .ALUControl(ALUControl), .ALUSrc(ALUSrc), .RegWrite(RegWrite), .MemRead(MemRead),
    .MemWrite(MemWrite), .ResultSrc(ResultSrc), .Branch(Branch), .Jump(Jump), .BranchType(BranchType));
  ImmediateGenerator immediategenerator_1 (
    .Instruction(DebugInstruction), .ImmType(ImmType), .Immediate(Imm32));  // open: Imm_S, Imm_I, Imm_B, Imm_U, Imm_J
  Multiplexer #(.width(32)) multiplexer_2 (.in0(RegB), .in1(Imm32), .out(ALUB), .sel(ALUSrc));
  Multiplexer #(.width(32)) multiplexer_3 (.in0(RegA), .in1(DebugPC), .out(multiplexer_3_out), .sel(isAUIPC));
  Multiplexer #(.width(32)) multiplexer_4 (
    .in0(DebugALUResult), .in1(MemReadData), .out(multiplexer_4_out), .sel(ResultSrc[0]));
  Multiplexer #(.width(32)) multiplexer_5 (.in0(multiplexer_3_out), .in1({32{1'b0}}), .out(ALUA), .sel(isLUI));
  Multiplexer #(.width(32)) multiplexer_6 (
    .in0(multiplexer_4_out), .in1(PCPlus4), .out(WriteBackData), .sel(ResultSrc[1]));
  Multiplexer #(.width(32)) multiplexer_7 (
    .in0(multiplexer_1_out), .in1(PCJALR), .out(multiplexer_7_out), .sel(selJALR));
  Multiplexer #(.width(32)) multiplexer_8 (.in0(multiplexer_7_out), .in1(PCImmTarget), .out(PCNext), .sel(BranchTaken));
  Adder #(.width(32)) adder_1 (.a(DebugPC), .b(32'h4), .out(PCPlus4), .cin(1'b0));  // open: cout
  Adder #(.width(32)) adder_2 (.a(DebugPC), .b(Imm32), .out(PCImmTarget), .cin(1'b0));  // open: cout
  Adder #(.width(32)) adder_3 (.a(RegA), .b(Imm32), .out(adder_3_out), .cin(1'b0));  // open: cout
  Comparator #(.width(32)) comparator_5 (.a(RegA), .b(RegB), .eq(Equal));  // open: gt, lt
  Comparator #(.width(1)) comparator_6 (.a(BranchType), .b(1'b0), .eq(isBEQ_type));  // open: gt, lt
  Comparator #(.width(1)) comparator_7 (.a(Equal), .b(1'b0), .eq(NotEqual));  // open: gt, lt
  assign PCJALR = adder_3_out & 32'hfffffffe;  // AND_Gate and_1, 32 bits wide
  RegisterFile registerfile_1 (
    .ReadReg1(DebugInstruction[19:15]), .ReadReg2(DebugInstruction[24:20]),
    .WriteReg(DebugInstruction[11:7]), .RegWrite(RegWrite), .WriteData(WriteBackData), .Clock(Clock),
    .ReadData1(RegA), .ReadData2(RegB));
  and and_2 (beq_cond, isBEQ_type, Equal);
  and and_3 (bne_cond, BranchType, NotEqual);
  or or_1 (branch_cond, beq_cond, bne_cond);
  and and_4 (BranchTaken, Branch, branch_cond);
  and and_5 (selJAL, Jump, isJAL);
  and and_6 (selJALR, Jump, isJALR);
  ALU alu_1 (.A(ALUA), .B(ALUB), .ALUControl(ALUControl), .Result(DebugALUResult));
  DataMemory datamemory_1 (
    .Address(DebugALUResult), .WriteData(RegB), .MemWrite(MemWrite), .Clock(Clock), .MemRead(MemRead),
    .ReadData(MemReadData));

  // Other names for the same wires on the sheet: ALUResult[31:0] = DebugALUResult;
  //   Instruction[31:0] = DebugInstruction; Opcode[6:0] = DebugInstruction[6:0]; rd[4:0] = DebugInstruction[11:7];
  //   funct3[2:0] = DebugInstruction[14:12]; rs1[4:0] = DebugInstruction[19:15]; rs2[4:0] = DebugInstruction[24:20];
  //   funct7[6:0] = DebugInstruction[31:25]; PCOut[31:0] = DebugPC
endmodule

module PipelineCPU (
  input  Clock,
  input  Reset,
  output [31:0] PCOut,
  output [31:0] Instruction,
  output [31:0] IFID_PC,
  output [31:0] IFID_Instruction,
  output [31:0] IDEX_PC,
  output [31:0] IDEX_Instruction,
  output [31:0] EXMEM_ALUResult,
  output [31:0] MEMWB_Result,
  output DebugRegWrite
);

  wire and_1_out, and_2_out, and_3_out, and_4_out, and_5_out, and_21_out, and_22_out, and_23_out, and_24_out,
       comparator_4_eq, comparator_5_eq, comparator_6_eq, comparator_7_eq, comparator_8_eq, comparator_9_eq,
       comparator_10_eq, comparator_11_eq, comparator_12_eq, EX_beq_cond, EX_bne_cond, EX_branch_cond,
       EX_BranchTaken, EX_Equal, EX_isAUIPC, EX_isBEQ_type, EX_isJALR, EX_isLUI, EX_NotEqual, EX_PCSrc,
       EX_selJALR, EXMEM_MemRead, EXMEM_MemWrite, EXMEM_rd_nz, EXMEM_RegWrite, EXMEM_valid_wb, Flush_IDEX,
       Flush_IFID, FwdA_MEM, FwdA_WB, FwdB_MEM, FwdB_WB, ID_ALUSrc, ID_Branch, ID_BranchType, ID_Jump,
       ID_MemRead, ID_MemWrite, ID_RegWrite, IDEX_ALUSrc, IDEX_Branch, IDEX_BranchType, IDEX_Jump,
       IDEX_MemRead, IDEX_MemWrite, IDEX_rd_nz, IDEX_RegWrite, IDEX_valid_load, IFIDWrite, Keep_IDEX, lu_eq1,
       lu_eq2, lu_match, MEMWB_rd_nz, MEMWB_valid_wb, NotReset, NotStall, Stall, WB_Bypass1, WB_Bypass2;
  wire [1:0] EXMEM_ResultSrc, ID_ResultSrc, IDEX_ResultSrc, MEMWB_ResultSrc, multiplexer_23_out;
  wire [2:0] ID_ImmType, IDEX_funct3;
  wire [3:0] ID_ALUControl, IDEX_ALUControl;
  wire [4:0] EXMEM_rd, IDEX_rd, IDEX_rs1, IDEX_rs2, MEMWB_rd, multiplexer_10_out, multiplexer_20_out,
       multiplexer_22_out;
  wire [6:0] IDEX_funct7, IDEX_opcode;
  wire [31:0] adder_3_out, EX_ALUA, EX_ALUB, EX_ALUResult, EX_OpA_Forwarded, EX_OpB_Forwarded,
       EX_PCImmTarget, EX_PCJALR, EX_TargetAddress, EXMEM_ForwardVal, EXMEM_PCPlus4, EXMEM_StoreData,
       ID_Immediate, ID_ReadData1, ID_ReadData2, IDEX_Immediate, IDEX_PCPlus4, IDEX_ReadData1,
       IDEX_ReadData2, IF_PCPlus4, IFID_PCPlus4, MEM_ReadData, MEMWB_ALUResult, MEMWB_PCPlus4,
       MEMWB_ReadData, multiplexer_1_out, multiplexer_2_out, multiplexer_3_out, multiplexer_4_out,
       multiplexer_8_out, multiplexer_9_out, multiplexer_11_out, multiplexer_12_out, multiplexer_13_out,
       multiplexer_19_out, multiplexer_24_out, PCNext, RF_ReadData1, RF_ReadData2;

  Multiplexer #(.width(32)) multiplexer_1 (.in0(IF_PCPlus4), .in1(PCOut), .out(multiplexer_1_out), .sel(Stall));
  Adder #(.width(32)) adder_1 (.a(PCOut), .b(32'h4), .out(IF_PCPlus4), .cin(1'b0));  // open: cout
  Register #(.width(32)) register_1 (.D(multiplexer_2_out), .en(IFIDWrite), .clk(Clock), .Q(IFID_PC));  // open: clr
  Multiplexer #(.width(32)) multiplexer_2 (.in0(PCOut), .in1({32{1'b0}}), .out(multiplexer_2_out), .sel(Flush_IFID));
  Register #(.width(32)) register_2 (
    .D(multiplexer_3_out), .en(IFIDWrite), .clk(Clock), .Q(IFID_Instruction));  // open: clr
  Multiplexer #(.width(32)) multiplexer_3 (.in0(Instruction), .in1(32'h13), .out(multiplexer_3_out), .sel(Flush_IFID));
  Register #(.width(32)) register_3 (
    .D(multiplexer_4_out), .en(IFIDWrite), .clk(Clock), .Q(IFID_PCPlus4));  // open: clr
  Multiplexer #(.width(32)) multiplexer_4 (
    .in0(IF_PCPlus4), .in1({32{1'b0}}), .out(multiplexer_4_out), .sel(Flush_IFID));
  Multiplexer #(.width(32)) multiplexer_5 (
    .in0(multiplexer_1_out), .in1(EX_TargetAddress), .out(PCNext), .sel(EX_PCSrc));
  PC pc_1 (.PCNext(PCNext), .Reset(Reset), .Clock(Clock), .PCOut(PCOut));
  InstructionMemory instructionmemory_1 (.Address(PCOut), .Instruction(Instruction));
  Multiplexer #(.width(32)) multiplexer_6 (
    .in0(RF_ReadData1), .in1(MEMWB_Result), .out(ID_ReadData1), .sel(WB_Bypass1));
  Multiplexer #(.width(32)) multiplexer_7 (
    .in0(RF_ReadData2), .in1(MEMWB_Result), .out(ID_ReadData2), .sel(WB_Bypass2));
  ControlUnit controlunit_1 (
    .Opcode(IFID_Instruction[6:0]), .Funct3(IFID_Instruction[14:12]), .Funct7(IFID_Instruction[31:25]),
    .ImmType(ID_ImmType), .ALUControl(ID_ALUControl), .ALUSrc(ID_ALUSrc), .RegWrite(ID_RegWrite),
    .MemRead(ID_MemRead), .MemWrite(ID_MemWrite), .ResultSrc(ID_ResultSrc), .Branch(ID_Branch),
    .Jump(ID_Jump), .BranchType(ID_BranchType));
  ImmediateGenerator immediategenerator_1 (
    .Instruction(IFID_Instruction), .ImmType(ID_ImmType), .Immediate(ID_Immediate));  // open: Imm_S, Imm_I, Imm_B, Imm_U, Imm_J
  RegisterFile registerfile_1 (
    .ReadReg1(IFID_Instruction[19:15]), .ReadReg2(IFID_Instruction[24:20]), .WriteReg(MEMWB_rd),
    .RegWrite(DebugRegWrite), .WriteData(MEMWB_Result), .Clock(Clock), .ReadData1(RF_ReadData1),
    .ReadData2(RF_ReadData2));
  Multiplexer #(.width(32)) multiplexer_8 (.in0(IFID_PC), .in1({32{1'b0}}), .out(multiplexer_8_out), .sel(Flush_IDEX));
  Multiplexer #(.width(32)) multiplexer_9 (
    .in0(IFID_Instruction), .in1(32'h13), .out(multiplexer_9_out), .sel(Flush_IDEX));
  Multiplexer #(.width(5)) multiplexer_10 (
    .in0(IFID_Instruction[11:7]), .in1({5{1'b0}}), .out(multiplexer_10_out), .sel(Flush_IDEX));
  and and_1 (and_1_out, ID_RegWrite, Keep_IDEX);
  and and_2 (and_2_out, ID_MemRead, Keep_IDEX);
  and and_3 (and_3_out, ID_MemWrite, Keep_IDEX);
  and and_4 (and_4_out, ID_Branch, Keep_IDEX);
  and and_5 (and_5_out, ID_Jump, Keep_IDEX);
  Register #(.width(32)) register_4 (.D(multiplexer_8_out), .clk(Clock), .Q(IDEX_PC));  // open: en, clr
  Register #(.width(32)) register_5 (.D(multiplexer_9_out), .clk(Clock), .Q(IDEX_Instruction));  // open: en, clr
  Register #(.width(32)) register_6 (.D(IFID_PCPlus4), .clk(Clock), .Q(IDEX_PCPlus4));  // open: en, clr
  Register #(.width(32)) register_7 (.D(ID_ReadData1), .clk(Clock), .Q(IDEX_ReadData1));  // open: en, clr
  Register #(.width(32)) register_8 (.D(ID_ReadData2), .clk(Clock), .Q(IDEX_ReadData2));  // open: en, clr
  Register #(.width(32)) register_9 (.D(ID_Immediate), .clk(Clock), .Q(IDEX_Immediate));  // open: en, clr
  Register #(.width(5)) register_10 (.D(IFID_Instruction[19:15]), .clk(Clock), .Q(IDEX_rs1));  // open: en, clr
  Register #(.width(5)) register_11 (.D(IFID_Instruction[24:20]), .clk(Clock), .Q(IDEX_rs2));  // open: en, clr
  Register #(.width(5)) register_12 (.D(multiplexer_10_out), .clk(Clock), .Q(IDEX_rd));  // open: en, clr
  Register #(.width(3)) register_13 (.D(IFID_Instruction[14:12]), .clk(Clock), .Q(IDEX_funct3));  // open: en, clr
  Register #(.width(7)) register_14 (.D(IFID_Instruction[31:25]), .clk(Clock), .Q(IDEX_funct7));  // open: en, clr
  Register #(.width(7)) register_15 (.D(IFID_Instruction[6:0]), .clk(Clock), .Q(IDEX_opcode));  // open: en, clr
  Register #(.width(4)) register_16 (.D(ID_ALUControl), .clk(Clock), .Q(IDEX_ALUControl));  // open: en, clr
  Register #(.width(1)) register_17 (.D(ID_ALUSrc), .clk(Clock), .Q(IDEX_ALUSrc));  // open: en, clr
  Register #(.width(1)) register_18 (.D(and_1_out), .clk(Clock), .Q(IDEX_RegWrite));  // open: en, clr
  Register #(.width(1)) register_19 (.D(and_2_out), .clk(Clock), .Q(IDEX_MemRead));  // open: en, clr
  Register #(.width(1)) register_20 (.D(and_3_out), .clk(Clock), .Q(IDEX_MemWrite));  // open: en, clr
  Register #(.width(2)) register_21 (.D(ID_ResultSrc), .clk(Clock), .Q(IDEX_ResultSrc));  // open: en, clr
  Register #(.width(1)) register_22 (.D(and_4_out), .clk(Clock), .Q(IDEX_Branch));  // open: en, clr
  Register #(.width(1)) register_23 (.D(and_5_out), .clk(Clock), .Q(IDEX_Jump));  // open: en, clr
  Register #(.width(1)) register_24 (.D(ID_BranchType), .clk(Clock), .Q(IDEX_BranchType));  // open: en, clr
  Multiplexer #(.width(32)) multiplexer_11 (
    .in0(IDEX_ReadData1), .in1(MEMWB_Result), .out(multiplexer_11_out), .sel(FwdA_WB));
  Multiplexer #(.width(32)) multiplexer_12 (
    .in0(IDEX_ReadData2), .in1(MEMWB_Result), .out(multiplexer_12_out), .sel(FwdB_WB));
  Comparator #(.width(7)) comparator_1 (.a(IDEX_opcode), .b(7'b0110111), .eq(EX_isLUI));  // open: gt, lt
  Comparator #(.width(7)) comparator_2 (.a(IDEX_opcode), .b(7'b0010111), .eq(EX_isAUIPC));  // open: gt, lt
  Comparator #(.width(7)) comparator_3 (.a(IDEX_opcode), .b(7'b1100111), .eq(EX_isJALR));  // open: gt, lt
  Multiplexer #(.width(32)) multiplexer_13 (
    .in0(EX_OpA_Forwarded), .in1(IDEX_PC), .out(multiplexer_13_out), .sel(EX_isAUIPC));
  Multiplexer #(.width(32)) multiplexer_14 (
    .in0(EX_OpB_Forwarded), .in1(IDEX_Immediate), .out(EX_ALUB), .sel(IDEX_ALUSrc));
  Comparator #(.width(5)) comparator_4 (.a(EXMEM_rd), .b({5{1'b0}}), .eq(comparator_4_eq));  // open: gt, lt
  Comparator #(.width(5)) comparator_5 (.a(MEMWB_rd), .b({5{1'b0}}), .eq(comparator_5_eq));  // open: gt, lt
  Comparator #(.width(5)) comparator_6 (.a(IDEX_rd), .b({5{1'b0}}), .eq(comparator_6_eq));  // open: gt, lt
  and and_6 (EXMEM_valid_wb, EXMEM_RegWrite, EXMEM_rd_nz);
  and and_7 (MEMWB_valid_wb, DebugRegWrite, MEMWB_rd_nz);
  Comparator #(.width(5)) comparator_7 (.a(EXMEM_rd), .b(IDEX_rs1), .eq(comparator_7_eq));  // open: gt, lt
  Comparator #(.width(5)) comparator_8 (.a(MEMWB_rd), .b(IDEX_rs1), .eq(comparator_8_eq));  // open: gt, lt
  Comparator #(.width(5)) comparator_9 (.a(EXMEM_rd), .b(IDEX_rs2), .eq(comparator_9_eq));  // open: gt, lt
  Comparator #(.width(5)) comparator_10 (.a(MEMWB_rd), .b(IDEX_rs2), .eq(comparator_10_eq));  // open: gt, lt
  Comparator #(.width(5)) comparator_11 (
    .a(MEMWB_rd), .b(IFID_Instruction[19:15]), .eq(comparator_11_eq));  // open: gt, lt
  Comparator #(.width(5)) comparator_12 (
    .a(MEMWB_rd), .b(IFID_Instruction[24:20]), .eq(comparator_12_eq));  // open: gt, lt
  Multiplexer #(.width(32)) multiplexer_15 (
    .in0(multiplexer_11_out), .in1(EXMEM_ForwardVal), .out(EX_OpA_Forwarded), .sel(FwdA_MEM));
  Multiplexer #(.width(32)) multiplexer_16 (
    .in0(multiplexer_12_out), .in1(EXMEM_ForwardVal), .out(EX_OpB_Forwarded), .sel(FwdB_MEM));
  Multiplexer #(.width(32)) multiplexer_17 (.in0(multiplexer_13_out), .in1({32{1'b0}}), .out(EX_ALUA), .sel(EX_isLUI));
  Comparator #(.width(1)) comparator_13 (.a(comparator_4_eq), .b(1'b0), .eq(EXMEM_rd_nz));  // open: gt, lt
  Comparator #(.width(1)) comparator_14 (.a(comparator_5_eq), .b(1'b0), .eq(MEMWB_rd_nz));  // open: gt, lt
  Comparator #(.width(1)) comparator_15 (.a(comparator_6_eq), .b(1'b0), .eq(IDEX_rd_nz));  // open: gt, lt
  and and_8 (FwdA_MEM, comparator_7_eq, EXMEM_valid_wb);
  and and_9 (FwdA_WB, comparator_8_eq, MEMWB_valid_wb);
  and and_10 (FwdB_MEM, comparator_9_eq, EXMEM_valid_wb);
  and and_11 (FwdB_WB, comparator_10_eq, MEMWB_valid_wb);
  and and_12 (WB_Bypass1, comparator_11_eq, MEMWB_valid_wb);
  and and_13 (WB_Bypass2, comparator_12_eq, MEMWB_valid_wb);
  Adder #(.width(32)) adder_2 (.a(IDEX_PC), .b(IDEX_Immediate), .out(EX_PCImmTarget), .cin(1'b0));  // open: cout
  Adder #(.width(32)) adder_3 (.a(EX_OpA_Forwarded), .b(IDEX_Immediate), .out(adder_3_out), .cin(1'b0));  // open: cout
  Multiplexer #(.width(32)) multiplexer_18 (
    .in0(EX_PCImmTarget), .in1(EX_PCJALR), .out(EX_TargetAddress), .sel(EX_selJALR));
  Comparator #(.width(32)) comparator_16 (.a(EX_OpA_Forwarded), .b(EX_OpB_Forwarded), .eq(EX_Equal));  // open: gt, lt
  Comparator #(.width(1)) comparator_17 (.a(IDEX_BranchType), .b(1'b0), .eq(EX_isBEQ_type));  // open: gt, lt
  Comparator #(.width(1)) comparator_18 (.a(EX_Equal), .b(1'b0), .eq(EX_NotEqual));  // open: gt, lt
  and and_14 (EX_beq_cond, EX_isBEQ_type, EX_Equal);
  and and_15 (EX_bne_cond, IDEX_BranchType, EX_NotEqual);
  or or_1 (EX_branch_cond, EX_beq_cond, EX_bne_cond);
  and and_16 (EX_BranchTaken, IDEX_Branch, EX_branch_cond);
  or or_2 (EX_PCSrc, EX_BranchTaken, IDEX_Jump);
  and and_17 (EX_selJALR, IDEX_Jump, EX_isJALR);
  assign EX_PCJALR = adder_3_out & 32'hfffffffe;  // AND_Gate and_18, 32 bits wide
  Comparator #(.width(5)) comparator_19 (.a(IDEX_rd), .b(IFID_Instruction[19:15]), .eq(lu_eq1));  // open: gt, lt
  Comparator #(.width(5)) comparator_20 (.a(IDEX_rd), .b(IFID_Instruction[24:20]), .eq(lu_eq2));  // open: gt, lt
  or or_3 (lu_match, lu_eq1, lu_eq2);
  and and_19 (IDEX_valid_load, IDEX_MemRead, IDEX_rd_nz);
  and and_20 (Stall, IDEX_valid_load, lu_match);
  or or_4 (Flush_IFID, Reset, EX_PCSrc);
  or or_5 (Flush_IDEX, Flush_IFID, Stall);
  Comparator #(.width(1)) comparator_21 (.a(Flush_IDEX), .b(1'b0), .eq(Keep_IDEX));  // open: gt, lt
  Comparator #(.width(1)) comparator_22 (.a(Stall), .b(1'b0), .eq(NotStall));  // open: gt, lt
  or or_6 (IFIDWrite, NotStall, Flush_IFID);
  Comparator #(.width(1)) comparator_23 (.a(Reset), .b(1'b0), .eq(NotReset));  // open: gt, lt
  ALU alu_1 (.A(EX_ALUA), .B(EX_ALUB), .ALUControl(IDEX_ALUControl), .Result(EX_ALUResult));
  Multiplexer #(.width(32)) multiplexer_19 (
    .in0(EX_ALUResult), .in1({32{1'b0}}), .out(multiplexer_19_out), .sel(Reset));
  Multiplexer #(.width(5)) multiplexer_20 (.in0(IDEX_rd), .in1({5{1'b0}}), .out(multiplexer_20_out), .sel(Reset));
  and and_21 (and_21_out, IDEX_RegWrite, NotReset);
  and and_22 (and_22_out, IDEX_MemRead, NotReset);
  and and_23 (and_23_out, IDEX_MemWrite, NotReset);
  Multiplexer #(.width(32)) multiplexer_21 (
    .in0(EXMEM_ALUResult), .in1(EXMEM_PCPlus4), .out(EXMEM_ForwardVal), .sel(EXMEM_ResultSrc[1]));
  Register #(.width(32)) register_25 (.D(multiplexer_19_out), .clk(Clock), .Q(EXMEM_ALUResult));  // open: en, clr
  Register #(.width(32)) register_26 (.D(EX_OpB_Forwarded), .clk(Clock), .Q(EXMEM_StoreData));  // open: en, clr
  Register #(.width(5)) register_27 (.D(multiplexer_20_out), .clk(Clock), .Q(EXMEM_rd));  // open: en, clr
  Register #(.width(1)) register_28 (.D(and_21_out), .clk(Clock), .Q(EXMEM_RegWrite));  // open: en, clr
  Register #(.width(1)) register_29 (.D(and_22_out), .clk(Clock), .Q(EXMEM_MemRead));  // open: en, clr
  Register #(.width(1)) register_30 (.D(and_23_out), .clk(Clock), .Q(EXMEM_MemWrite));  // open: en, clr
  Register #(.width(2)) register_31 (.D(IDEX_ResultSrc), .clk(Clock), .Q(EXMEM_ResultSrc));  // open: en, clr
  Register #(.width(32)) register_32 (.D(IDEX_PCPlus4), .clk(Clock), .Q(EXMEM_PCPlus4));  // open: en, clr
  DataMemory datamemory_1 (
    .Address(EXMEM_ALUResult), .WriteData(EXMEM_StoreData), .MemWrite(EXMEM_MemWrite), .Clock(Clock),
    .MemRead(EXMEM_MemRead), .ReadData(MEM_ReadData));
  Multiplexer #(.width(5)) multiplexer_22 (.in0(EXMEM_rd), .in1({5{1'b0}}), .out(multiplexer_22_out), .sel(Reset));
  and and_24 (and_24_out, EXMEM_RegWrite, NotReset);
  Multiplexer #(.width(2)) multiplexer_23 (.in0(EXMEM_ResultSrc), .in1(2'b00), .out(multiplexer_23_out), .sel(Reset));
  Multiplexer #(.width(32)) multiplexer_24 (
    .in0(MEMWB_ALUResult), .in1(MEMWB_ReadData), .out(multiplexer_24_out), .sel(MEMWB_ResultSrc[0]));
  Register #(.width(32)) register_33 (.D(EXMEM_ALUResult), .clk(Clock), .Q(MEMWB_ALUResult));  // open: en, clr
  Register #(.width(32)) register_34 (.D(MEM_ReadData), .clk(Clock), .Q(MEMWB_ReadData));  // open: en, clr
  Register #(.width(32)) register_35 (.D(EXMEM_PCPlus4), .clk(Clock), .Q(MEMWB_PCPlus4));  // open: en, clr
  Register #(.width(5)) register_36 (.D(multiplexer_22_out), .clk(Clock), .Q(MEMWB_rd));  // open: en, clr
  Register #(.width(1)) register_37 (.D(and_24_out), .clk(Clock), .Q(DebugRegWrite));  // open: en, clr
  Register #(.width(2)) register_38 (.D(multiplexer_23_out), .clk(Clock), .Q(MEMWB_ResultSrc));  // open: en, clr
  Multiplexer #(.width(32)) multiplexer_25 (
    .in0(multiplexer_24_out), .in1(MEMWB_PCPlus4), .out(MEMWB_Result), .sel(MEMWB_ResultSrc[1]));

  // Other names for the same wires on the sheet: ID_opcode[6:0] = IFID_Instruction[6:0];
  //   ID_rd[4:0] = IFID_Instruction[11:7]; ID_funct3[2:0] = IFID_Instruction[14:12];
  //   ID_rs1[4:0] = IFID_Instruction[19:15]; ID_rs2[4:0] = IFID_Instruction[24:20];
  //   ID_funct7[6:0] = IFID_Instruction[31:25]; MEMWB_RegWrite = DebugRegWrite
endmodule
