// Logisim project RISC_V_CPU_32_backup.circ as structural Verilog
module ALU (
  input  [31:0] A,
  input  [31:0] B,
  input  [3:0] ALUControl,
  output [31:0] Result
);

  wire comparator_1_lt, comparator_2_lt;
  wire [31:0] adder_1_out, and_1_out, multiplexer_1_out, multiplexer_2_out, or_1_out, shifter_1_out,
       shifter_2_out, shifter_3_out, subtractor_1_out, xor_1_out;

  Adder #(.width(32)) adder_1 (.a(A), .b(B), .out(adder_1_out), .cin(1'b0));  // open: cout
  Subtractor #(.width(32)) subtractor_1 (.a(A), .b(B), .out(subtractor_1_out), .bin(1'b0));  // open: bout
  assign and_1_out = A & B;  // AND_Gate and_1, 32 bits wide
  assign or_1_out = A | B;  // OR_Gate or_1, 32 bits wide
  assign xor_1_out = A ^ B;  // XOR_Gate xor_1, 32 bits wide
  Comparator #(.width(32)) comparator_1 (.a(A), .b(B), .lt(comparator_1_lt));  // open: gt, eq
  Comparator #(.mode("unsigned"), .width(32)) comparator_2 (.a(A), .b(B), .lt(comparator_2_lt));  // open: gt, eq
  Shifter #(.width(32)) shifter_1 (.in(A), .\dist (B[4:0]), .out(shifter_1_out));
  Shifter #(.shift("lr"), .width(32)) shifter_2 (.in(A), .\dist (B[4:0]), .out(shifter_2_out));
  Shifter #(.shift("ar"), .width(32)) shifter_3 (.in(A), .\dist (B[4:0]), .out(shifter_3_out));
  Multiplexer #(.width(32)) multiplexer_1 (
    .in0({32{1'b0}}), .in1(32'h1), .out(multiplexer_1_out), .sel(comparator_1_lt));
  Multiplexer #(.width(32)) multiplexer_2 (
    .in0({32{1'b0}}), .in1(32'h1), .out(multiplexer_2_out), .sel(comparator_2_lt));
  Multiplexer #(.select(4), .width(32)) multiplexer_3 (
    .in0(adder_1_out), .in1(subtractor_1_out), .in2(and_1_out), .in3(or_1_out), .in4(xor_1_out),
    .in5(multiplexer_1_out), .in6(multiplexer_2_out), .in7(shifter_1_out), .in8(shifter_2_out),
    .in9(shifter_3_out), .in10({32{1'b0}}), .in11({32{1'b0}}), .in12({32{1'b0}}), .in13({32{1'b0}}),
    .in14({32{1'b0}}), .in15({32{1'b0}}), .out(Result), .sel(ALUControl));

  // Notes on the sheet:
  //   ALUControl: initial=0x9
  //   A: initial=0xffffffffffffffec
  //   B: initial=0x2
endmodule

module RegisterFile (
  input  [4:0] ReadReg1,
  input  [4:0] ReadReg2,
  input  [4:0] WriteReg,
  input  RegWrite,
  input  [31:0] WriteData,
  input  Clock,
  output [31:0] ReadData1,
  output [31:0] ReadData2
);

  wire decoder_1_out1, decoder_1_out2, decoder_1_out3, decoder_1_out4, decoder_1_out6, decoder_1_out7,
       decoder_1_out8, decoder_1_out9, decoder_1_out10, decoder_1_out11;

  Decoder #(.select(5)) decoder_1 (
    .out1(decoder_1_out1), .out2(decoder_1_out2), .out3(decoder_1_out3), .out4(decoder_1_out4), .out5(Clock),
    .out6(decoder_1_out6), .out7(decoder_1_out7), .out8(decoder_1_out8), .out9(decoder_1_out9),
    .out10(decoder_1_out10), .out11(decoder_1_out11), .out12(decoder_1_out11), .sel(WriteReg), .en(RegWrite));  // open: out0, out13, out14, out15, out16, out17, out18, out19, out20, out21, out22, out23, out24, out25, out26, out27, out28, out29, out30, out31
  Register #(.width(32)) register_1 (.D(WriteData), .en(decoder_1_out1), .clk(Clock), .clr(decoder_1_out7));  // open: Q
  Register #(.width(32)) register_2 (.D(WriteData), .en(decoder_1_out2), .clk(Clock));  // open: Q, clr
  Register #(.width(32)) register_3 (.D(WriteData), .en(decoder_1_out3), .clk(Clock));  // open: Q, clr
  Register #(.width(32)) register_4 (.D(WriteData), .en(decoder_1_out4), .clk(Clock));  // open: Q, clr
  Register #(.width(32)) register_5 (.D(WriteData), .en(Clock), .clk(Clock));  // open: Q, clr
  Register #(.width(32)) register_6 (.D(WriteData), .en(decoder_1_out6), .clk(Clock));  // open: Q, clr
  Register #(.width(32)) register_7 (.D(WriteData), .en(decoder_1_out7), .clk(Clock));  // open: Q, clr
  Register #(.width(32)) register_8 (.D(WriteData), .en(decoder_1_out8), .clk(Clock));  // open: Q, clr
  Register #(.width(32)) register_9 (.D(WriteData), .en(decoder_1_out9), .clk(Clock));  // open: Q, clr
  Register #(.width(32)) register_10 (.D(WriteData), .en(decoder_1_out10), .clk(Clock));  // open: Q, clr
  Register #(.width(32)) register_11 (.D(WriteData), .en(decoder_1_out11), .clk(Clock));  // open: Q, clr
  Register #(.width(32)) register_12 (.D(WriteData), .en(decoder_1_out11), .clk(Clock));  // open: Q, clr
  Register #(.width(32)) register_13 (.D(WriteData), .clk(Clock));  // open: en, Q, clr
  Register #(.width(32)) register_14 (.D(WriteData), .clk(Clock));  // open: en, Q, clr
  Register #(.width(32)) register_15 (.D(WriteData), .clk(Clock));  // open: en, Q, clr
  Register #(.width(32)) register_16 (.D(WriteData), .clk(Clock));  // open: en, Q, clr
  Register #(.width(32)) register_17 (.D(WriteData), .clk(Clock));  // open: en, Q, clr
  Register #(.width(32)) register_18 (.D(WriteData), .clk(Clock));  // open: en, Q, clr
  Register #(.width(32)) register_19 (.D(WriteData), .clk(Clock));  // open: en, Q, clr
  Register #(.width(32)) register_20 (.D(WriteData), .clk(Clock));  // open: en, Q, clr
  Register #(.width(32)) register_21 (.D(WriteData), .clk(Clock));  // open: en, Q, clr
  Register #(.width(32)) register_22 (.D(WriteData), .clk(Clock));  // open: en, Q, clr
  Register #(.width(32)) register_23 (.D(WriteData), .clk(Clock));  // open: en, Q, clr
  Register #(.width(32)) register_24 (.D(WriteData), .clk(Clock));  // open: en, Q, clr
  Register #(.width(32)) register_25 (.D(WriteData), .clk(Clock));  // open: en, Q, clr
  Register #(.width(32)) register_26 (.D(WriteData), .clk(Clock));  // open: en, Q, clr
  Register #(.width(32)) register_27 (.D(WriteData), .clk(Clock));  // open: en, Q, clr
  Register #(.width(32)) register_28 (.D(WriteData), .clk(Clock));  // open: en, Q, clr
  Register #(.width(32)) register_29 (.D(WriteData), .clk(Clock));  // open: en, Q, clr
  Register #(.width(32)) register_30 (.D(WriteData), .clk(Clock));  // open: en, Q, clr
  Register #(.width(32)) register_31 (.D(WriteData), .clk(Clock));  // open: en, Q, clr
endmodule
