// Logisim project RISC_V_CPU_32_backup_v2.circ as structural Verilog
module ALU (
  input  [31:0] A,
  input  [31:0] B,
  input  [3:0] ALUControl,
  output [31:0] Result
);

  wire comparator_1_lt, comparator_2_lt;
  wire [31:0] adder_1_out, and_1_out, multiplexer_1_out, multiplexer_2_out, or_1_out, shifter_1_out,
       shifter_2_out, shifter_3_out, subtractor_1_out, xor_1_out;

  Adder #(.width(32)) adder_1 (.a(A), .b(B), .out(adder_1_out), .cin(1'b0));  // open: cout
  Subtractor #(.width(32)) subtractor_1 (.a(A), .b(B), .out(subtractor_1_out), .bin(1'b0));  // open: bout
  assign and_1_out = A & B;  // AND_Gate and_1, 32 bits wide
  assign or_1_out = A | B;  // OR_Gate or_1, 32 bits wide
  assign xor_1_out = A ^ B;  // XOR_Gate xor_1, 32 bits wide
  Comparator #(.width(32)) comparator_1 (.a(A), .b(B), .lt(comparator_1_lt));  // open: gt, eq
  Comparator #(.mode("unsigned"), .width(32)) comparator_2 (.a(A), .b(B), .lt(comparator_2_lt));  // open: gt, eq
  Shifter #(.width(32)) shifter_1 (.in(A), .\dist (B[4:0]), .out(shifter_1_out));
  Shifter #(.shift("lr"), .width(32)) shifter_2 (.in(A), .\dist (B[4:0]), .out(shifter_2_out));
  Shifter #(.shift("ar"), .width(32)) shifter_3 (.in(A), .\dist (B[4:0]), .out(shifter_3_out));
  Multiplexer #(.width(32)) multiplexer_1 (
    .in0({32{1'b0}}), .in1(32'h1), .out(multiplexer_1_out), .sel(comparator_1_lt));
  Multiplexer #(.width(32)) multiplexer_2 (
    .in0({32{1'b0}}), .in1(32'h1), .out(multiplexer_2_out), .sel(comparator_2_lt));
  Multiplexer #(.select(4), .width(32)) multiplexer_3 (
    .in0(adder_1_out), .in1(subtractor_1_out), .in2(and_1_out), .in3(or_1_out), .in4(xor_1_out),
    .in5(multiplexer_1_out), .in6(multiplexer_2_out), .in7(shifter_1_out), .in8(shifter_2_out),
    .in9(shifter_3_out), .in10({32{1'b0}}), .in11({32{1'b0}}), .in12({32{1'b0}}), .in13({32{1'b0}}),
    .in14({32{1'b0}}), .in15({32{1'b0}}), .out(Result), .sel(ALUControl));

  // Notes on the sheet:
  //   ALUControl: initial=0x9
  //   A: initial=0xffffffffffffffec
  //   B: initial=0x2
endmodule

module RegisterFile (
  input  [4:0] ReadReg1,
  input  [4:0] ReadReg2,
  input  [4:0] WriteReg,
  input  RegWrite,
  input  [31:0] WriteData,
  input  Clock,
  output [31:0] ReadData1,
  output [31:0] ReadData2
);

  wire WE1, WE2, WE3, WE4, WE5, WE6, WE7, WE8, WE9, WE10, WE11, WE12, WE13, WE14, WE15, WE16, WE17, WE18,
       WE19, WE20, WE21, WE22, WE23, WE24, WE25, WE26, WE27, WE28, WE29, WE30, WE31;
  wire [31:0] R1, R5, R9, R13, R17, R21, R25, R29;

  Decoder #(.select(5)) decoder_1 (
    .out2(WE1), .out3(WE2), .out4(WE3), .out5(WE4), .out6(WE5), .out7(WE6), .out8(WE7), .out9(WE8),
    .out10(WE9), .out11(WE10), .out12(WE11), .out13(WE12), .out14(WE13), .out15(WE14), .out16(WE15),
    .out17(WE16), .out18(WE17), .out19(WE18), .out20(WE19), .out21(WE20), .out22(WE21), .out23(WE22),
    .out24(WE23), .out25(WE24), .out26(WE25), .out27(WE26), .out28(WE27), .out29(WE28), .out30(WE29),
    .out31(WE30), .sel(WriteReg), .en(RegWrite));  // open: out0, out1
  Register #(.width(32)) register_1 (.D(WriteData), .en(WE1), .clk(Clock), .Q(R1));  // open: clr
  Register #(.width(32)) register_2 (.D(WriteData), .en(WE2), .clk(Clock), .Q(R1));  // open: clr
  Register #(.width(32)) register_3 (.D(WriteData), .en(WE3), .clk(Clock), .Q(R1));  // open: clr
  Register #(.width(32)) register_4 (.D(WriteData), .en(WE4), .clk(Clock), .Q(R1));  // open: clr
  Register #(.width(32)) register_5 (.D(WriteData), .en(WE5), .clk(Clock), .Q(R5));  // open: clr
  Register #(.width(32)) register_6 (.D(WriteData), .en(WE6), .clk(Clock), .Q(R5));  // open: clr
  Register #(.width(32)) register_7 (.D(WriteData), .en(WE7), .clk(Clock), .Q(R5));  // open: clr
  Register #(.width(32)) register_8 (.D(WriteData), .en(WE8), .clk(Clock), .Q(R5));  // open: clr
  Register #(.width(32)) register_9 (.D(WriteData), .en(WE9), .clk(Clock), .Q(R9));  // open: clr
  Register #(.width(32)) register_10 (.D(WriteData), .en(WE10), .clk(Clock), .Q(R9));  // open: clr
  Register #(.width(32)) register_11 (.D(WriteData), .en(WE11), .clk(Clock), .Q(R9));  // open: clr
  Register #(.width(32)) register_12 (.D(WriteData), .en(WE12), .clk(Clock), .Q(R9));  // open: clr
  Register #(.width(32)) register_13 (.D(WriteData), .en(WE13), .clk(Clock), .Q(R13));  // open: clr
  Register #(.width(32)) register_14 (.D(WriteData), .en(WE14), .clk(Clock), .Q(R13));  // open: clr
  Register #(.width(32)) register_15 (.D(WriteData), .en(WE15), .clk(Clock), .Q(R13));  // open: clr
  Register #(.width(32)) register_16 (.D(WriteData), .en(WE16), .clk(Clock), .Q(R13));  // open: clr
  Register #(.width(32)) register_17 (.D(WriteData), .en(WE17), .clk(Clock), .Q(R17));  // open: clr
  Register #(.width(32)) register_18 (.D(WriteData), .en(WE18), .clk(Clock), .Q(R17));  // open: clr
  Register #(.width(32)) register_19 (.D(WriteData), .en(WE19), .clk(Clock), .Q(R17));  // open: clr
  Register #(.width(32)) register_20 (.D(WriteData), .en(WE20), .clk(Clock), .Q(R17));  // open: clr
  Register #(.width(32)) register_21 (.D(WriteData), .en(WE21), .clk(Clock), .Q(R21));  // open: clr
  Register #(.width(32)) register_22 (.D(WriteData), .en(WE22), .clk(Clock), .Q(R21));  // open: clr
  Register #(.width(32)) register_23 (.D(WriteData), .en(WE23), .clk(Clock), .Q(R21));  // open: clr
  Register #(.width(32)) register_24 (.D(WriteData), .en(WE24), .clk(Clock), .Q(R21));  // open: clr
  Register #(.width(32)) register_25 (.D(WriteData), .en(WE25), .clk(Clock), .Q(R25));  // open: clr
  Register #(.width(32)) register_26 (.D(WriteData), .en(WE26), .clk(Clock), .Q(R25));  // open: clr
  Register #(.width(32)) register_27 (.D(WriteData), .en(WE27), .clk(Clock), .Q(R25));  // open: clr
  Register #(.width(32)) register_28 (.D(WriteData), .en(WE28), .clk(Clock), .Q(R25));  // open: clr
  Register #(.width(32)) register_29 (.D(WriteData), .en(WE29), .clk(Clock), .Q(R29));  // open: clr
  Register #(.width(32)) register_30 (.D(WriteData), .en(WE30), .clk(Clock), .Q(R29));  // open: clr
  Register #(.width(32)) register_31 (.D(WriteData), .en(WE31), .clk(Clock), .Q(R29));  // open: clr
  Multiplexer #(.select(5), .width(32)) multiplexer_1 (
    .in0({32{1'b0}}), .in1(R1), .in2(R1), .in3(R1), .in4(R1), .in5(R5), .in6(R5), .in7(R5), .in8(R5),
    .in9(R9), .in10(R9), .in11(R9), .in12(R9), .in13(R13), .in14(R13), .in15(R13), .in16(R13), .in17(R17),
    .in18(R17), .in19(R17), .in20(R17), .in21(R21), .in22(R21), .in23(R21), .in24(R25), .in25(R25),
    .in26(R25), .in27(R25), .in28(R29), .in29(R29), .in30(R29), .in31(R21), .out(ReadData1), .sel(ReadReg1));

  // Other names for the same wires on the sheet: R2[31:0] = R1; R3[31:0] = R1; R4[31:0] = R1; R6[31:0] = R5;
  //   R7[31:0] = R5; R8[31:0] = R5; R10[31:0] = R9; R11[31:0] = R9; R12[31:0] = R9; R14[31:0] = R13; R15[31:0] = R13;
  //   R16[31:0] = R13; R18[31:0] = R17; R19[31:0] = R17; R20[31:0] = R17; R22[31:0] = R21; R23[31:0] = R21;
  //   R24[31:0] = R21; R26[31:0] = R25; R27[31:0] = R25; R28[31:0] = R25; R30[31:0] = R29; R31[31:0] = R29
endmodule
