// Logisim project RISC_V_CPU_32_backup_v4.circ as structural Verilog
module ALU (
  input  [31:0] A,
  input  [31:0] B,
  input  [3:0] ALUControl,
  output [31:0] Result
);

  wire comparator_1_lt, comparator_2_lt;
  wire [31:0] adder_1_out, and_1_out, multiplexer_1_out, multiplexer_2_out, or_1_out, shifter_1_out,
       shifter_2_out, shifter_3_out, subtractor_1_out, xor_1_out;

  Adder #(.width(32)) adder_1 (.a(A), .b(B), .out(adder_1_out), .cin(1'b0));  // open: cout
  Subtractor #(.width(32)) subtractor_1 (.a(A), .b(B), .out(subtractor_1_out), .bin(1'b0));  // open: bout
  assign and_1_out = A & B;  // AND_Gate and_1, 32 bits wide
  assign or_1_out = A | B;  // OR_Gate or_1, 32 bits wide
  assign xor_1_out = A ^ B;  // XOR_Gate xor_1, 32 bits wide
  Comparator #(.width(32)) comparator_1 (.a(A), .b(B), .lt(comparator_1_lt));  // open: gt, eq
  Comparator #(.mode("unsigned"), .width(32)) comparator_2 (.a(A), .b(B), .lt(comparator_2_lt));  // open: gt, eq
  Shifter #(.width(32)) shifter_1 (.in(A), .\dist (B[4:0]), .out(shifter_1_out));
  Shifter #(.shift("lr"), .width(32)) shifter_2 (.in(A), .\dist (B[4:0]), .out(shifter_2_out));
  Shifter #(.shift("ar"), .width(32)) shifter_3 (.in(A), .\dist (B[4:0]), .out(shifter_3_out));
  Multiplexer #(.width(32)) multiplexer_1 (
    .in0({32{1'b0}}), .in1(32'h1), .out(multiplexer_1_out), .sel(comparator_1_lt));
  Multiplexer #(.width(32)) multiplexer_2 (
    .in0({32{1'b0}}), .in1(32'h1), .out(multiplexer_2_out), .sel(comparator_2_lt));
  Multiplexer #(.select(4), .width(32)) multiplexer_3 (
    .in0(adder_1_out), .in1(subtractor_1_out), .in2(and_1_out), .in3(or_1_out), .in4(xor_1_out),
    .in5(multiplexer_1_out), .in6(multiplexer_2_out), .in7(shifter_1_out), .in8(shifter_2_out),
    .in9(shifter_3_out), .in10({32{1'b0}}), .in11({32{1'b0}}), .in12({32{1'b0}}), .in13({32{1'b0}}),
    .in14({32{1'b0}}), .in15({32{1'b0}}), .out(Result), .sel(ALUControl));

  // Notes on the sheet:
  //   ALUControl: initial=0x9
  //   B: initial=0x2
endmodule

module RegisterFile (
  input  [4:0] ReadReg1,
  input  [4:0] ReadReg2,
  input  [4:0] WriteReg,
  input  RegWrite,
  input  [31:0] WriteData,
  input  Clock,
  output [31:0] ReadData1,
  output [31:0] ReadData2
);

  wire WE1, WE2, WE3, WE4, WE5, WE6, WE7, WE8, WE9, WE10, WE11, WE12, WE13, WE14, WE15, WE16, WE17, WE18,
       WE19, WE20, WE21, WE22, WE23, WE24, WE25, WE26, WE27, WE28, WE29, WE30, WE31;
  wire [31:0] R1, R2, R3, R4, R5, R6, R7, R8, R9, R10, R11, R12, R13, R14, R15, R16, R17, R18, R19, R20, R21,
       R22, R23, R24, R25, R26, R27, R28, R29, R30, R31;

  Decoder #(.select(5)) decoder_1 (
    .out1(WE1), .out2(WE2), .out3(WE3), .out4(WE4), .out5(WE5), .out6(WE6), .out7(WE7), .out8(WE8),
    .out9(WE9), .out10(WE10), .out11(WE11), .out12(WE12), .out13(WE13), .out14(WE14), .out15(WE15),
    .out16(WE16), .out17(WE17), .out18(WE18), .out19(WE19), .out20(WE20), .out21(WE21), .out22(WE22),
    .out23(WE23), .out24(WE24), .out25(WE25), .out26(WE26), .out27(WE27), .out28(WE28), .out29(WE29),
    .out30(WE30), .out31(WE31), .sel(WriteReg), .en(RegWrite));  // open: out0
  Register #(.width(32)) register_1 (.D(WriteData), .en(WE1), .clk(Clock), .Q(R1));  // open: clr
  Register #(.width(32)) register_2 (.D(WriteData), .en(WE2), .clk(Clock), .Q(R2));  // open: clr
  Register #(.width(32)) register_3 (.D(WriteData), .en(WE3), .clk(Clock), .Q(R3));  // open: clr
  Register #(.width(32)) register_4 (.D(WriteData), .en(WE4), .clk(Clock), .Q(R4));  // open: clr
  Register #(.width(32)) register_5 (.D(WriteData), .en(WE5), .clk(Clock), .Q(R5));  // open: clr
  Register #(.width(32)) register_6 (.D(WriteData), .en(WE6), .clk(Clock), .Q(R6));  // open: clr
  Register #(.width(32)) register_7 (.D(WriteData), .en(WE7), .clk(Clock), .Q(R7));  // open: clr
  Register #(.width(32)) register_8 (.D(WriteData), .en(WE8), .clk(Clock), .Q(R8));  // open: clr
  Register #(.width(32)) register_9 (.D(WriteData), .en(WE9), .clk(Clock), .Q(R9));  // open: clr
  Register #(.width(32)) register_10 (.D(WriteData), .en(WE10), .clk(Clock), .Q(R10));  // open: clr
  Register #(.width(32)) register_11 (.D(WriteData), .en(WE11), .clk(Clock), .Q(R11));  // open: clr
  Register #(.width(32)) register_12 (.D(WriteData), .en(WE12), .clk(Clock), .Q(R12));  // open: clr
  Register #(.width(32)) register_13 (.D(WriteData), .en(WE13), .clk(Clock), .Q(R13));  // open: clr
  Register #(.width(32)) register_14 (.D(WriteData), .en(WE14), .clk(Clock), .Q(R14));  // open: clr
  Register #(.width(32)) register_15 (.D(WriteData), .en(WE15), .clk(Clock), .Q(R15));  // open: clr
  Register #(.width(32)) register_16 (.D(WriteData), .en(WE16), .clk(Clock), .Q(R16));  // open: clr
  Register #(.width(32)) register_17 (.D(WriteData), .en(WE17), .clk(Clock), .Q(R17));  // open: clr
  Register #(.width(32)) register_18 (.D(WriteData), .en(WE18), .clk(Clock), .Q(R18));  // open: clr
  Register #(.width(32)) register_19 (.D(WriteData), .en(WE19), .clk(Clock), .Q(R19));  // open: clr
  Register #(.width(32)) register_20 (.D(WriteData), .en(WE20), .clk(Clock), .Q(R20));  // open: clr
  Register #(.width(32)) register_21 (.D(WriteData), .en(WE21), .clk(Clock), .Q(R21));  // open: clr
  Register #(.width(32)) register_22 (.D(WriteData), .en(WE22), .clk(Clock), .Q(R22));  // open: clr
  Register #(.width(32)) register_23 (.D(WriteData), .en(WE23), .clk(Clock), .Q(R23));  // open: clr
  Register #(.width(32)) register_24 (.D(WriteData), .en(WE24), .clk(Clock), .Q(R24));  // open: clr
  Register #(.width(32)) register_25 (.D(WriteData), .en(WE25), .clk(Clock), .Q(R25));  // open: clr
  Register #(.width(32)) register_26 (.D(WriteData), .en(WE26), .clk(Clock), .Q(R26));  // open: clr
  Register #(.width(32)) register_27 (.D(WriteData), .en(WE27), .clk(Clock), .Q(R27));  // open: clr
  Register #(.width(32)) register_28 (.D(WriteData), .en(WE28), .clk(Clock), .Q(R28));  // open: clr
  Register #(.width(32)) register_29 (.D(WriteData), .en(WE29), .clk(Clock), .Q(R29));  // open: clr
  Register #(.width(32)) register_30 (.D(WriteData), .en(WE30), .clk(Clock), .Q(R30));  // open: clr
  Register #(.width(32)) register_31 (.D(WriteData), .en(WE31), .clk(Clock), .Q(R31));  // open: clr
  Multiplexer #(.select(5), .width(32)) multiplexer_1 (
    .in0({32{1'b0}}), .in1(R1), .in2(R2), .in3(R3), .in4(R4), .in5(R5), .in6(R6), .in7(R7), .in8(R8),
    .in9(R9), .in10(R10), .in11(R11), .in12(R12), .in13(R13), .in14(R14), .in15(R15), .in16(R16), .in17(R17),
    .in18(R18), .in19(R19), .in20(R20), .in21(R21), .in22(R22), .in23(R23), .in24(R24), .in25(R25),
    .in26(R26), .in27(R27), .in28(R28), .in29(R29), .in30(R30), .in31(R31), .out(ReadData1), .sel(ReadReg1));
  Multiplexer #(.select(5), .width(32)) multiplexer_2 (
    .in0({32{1'b0}}), .in1(R1), .in2(R2), .in3(R3), .in4(R4), .in5(R5), .in6(R6), .in7(R7), .in8(R8),
    .in9(R9), .in10(R10), .in11(R11), .in12(R12), .in13(R13), .in14(R14), .in15(R15), .in16(R16), .in17(R17),
    .in18(R18), .in19(R19), .in20(R20), .in21(R21), .in22(R22), .in23(R23), .in24(R24), .in25(R25),
    .in26(R26), .in27(R27), .in28(R28), .in29(R29), .in30(R30), .in31(R31), .out(ReadData2), .sel(ReadReg2));

  // Other names for the same wires on the sheet: OUT1[31:0] = ReadData1; OUT2[31:0] = ReadData2; SEL1[4:0] = ReadReg1;
  //   SEL2[4:0] = ReadReg2

  // Notes on the sheet:
  //   RegWrite: initial=0x1
  //   WriteData: initial=0x7b
  //   WriteReg: initial=0x1
endmodule

module ImmediateGenerator (
  input  [31:0] Instruction,
  input  [2:0] ImmType,
  output [31:0] Immediate,
  output [31:0] Imm_S,
  output [31:0] Imm_I,
  output [31:0] Imm_B,
  output [31:0] Imm_U,
  output [31:0] Imm_J
);

  assign Imm_I = {{20{Instruction[31]}}, Instruction[31:20]};  // Bit_Extender bit_extender_1
  Multiplexer #(.select(3), .width(32)) multiplexer_1 (
    .in0(Imm_I), .in1(Imm_S), .in2(Imm_B), .in3({Instruction[31:12], {12{1'b0}}}), .in4(Imm_J),
    .in5({32{1'b0}}), .in6({32{1'b0}}), .in7({32{1'b0}}), .out(Immediate), .sel(ImmType));
  assign Imm_S = {{20{Instruction[31]}}, {Instruction[31:25], Instruction[11:7]}};  // Bit_Extender bit_extender_2
  assign Imm_B = {{19{Instruction[31]}}, {Instruction[31], Instruction[7], Instruction[30:25], Instruction[11:8], 1'b0}};  // Bit_Extender bit_extender_3
  assign Imm_J = {{11{Instruction[31]}}, {Instruction[31], Instruction[19:12], Instruction[20], Instruction[30:21], 1'b0}};  // Bit_Extender bit_extender_4

  assign Imm_U = {Instruction[31:12], {12{1'b0}}};

  // Notes on the sheet:
  //   Instruction: initial=0xef
  //   ImmType: initial=0x4
endmodule
