// Logisim project RISC_V_CPU_32_backupp_v6.circ as structural Verilog
module ALU (
  input  [31:0] A,
  input  [31:0] B,
  input  [3:0] ALUControl,
  output [31:0] Result
);

  wire comparator_1_lt, comparator_2_lt;
  wire [31:0] adder_1_out, and_1_out, multiplexer_1_out, multiplexer_2_out, or_1_out, shifter_1_out,
       shifter_2_out, shifter_3_out, subtractor_1_out, xor_1_out;

  Adder #(.width(32)) adder_1 (.a(A), .b(B), .out(adder_1_out), .cin(1'b0));  // open: cout
  Subtractor #(.width(32)) subtractor_1 (.a(A), .b(B), .out(subtractor_1_out), .bin(1'b0));  // open: bout
  assign and_1_out = A & B;  // AND_Gate and_1, 32 bits wide
  assign or_1_out = A | B;  // OR_Gate or_1, 32 bits wide
  assign xor_1_out = A ^ B;  // XOR_Gate xor_1, 32 bits wide
  Comparator #(.width(32)) comparator_1 (.a(A), .b(B), .lt(comparator_1_lt));  // open: gt, eq
  Comparator #(.mode("unsigned"), .width(32)) comparator_2 (.a(A), .b(B), .lt(comparator_2_lt));  // open: gt, eq
  Shifter #(.width(32)) shifter_1 (.in(A), .\dist (B[4:0]), .out(shifter_1_out));
  Shifter #(.shift("lr"), .width(32)) shifter_2 (.in(A), .\dist (B[4:0]), .out(shifter_2_out));
  Shifter #(.shift("ar"), .width(32)) shifter_3 (.in(A), .\dist (B[4:0]), .out(shifter_3_out));
  Multiplexer #(.width(32)) multiplexer_1 (
    .in0({32{1'b0}}), .in1(32'h1), .out(multiplexer_1_out), .sel(comparator_1_lt));
  Multiplexer #(.width(32)) multiplexer_2 (
    .in0({32{1'b0}}), .in1(32'h1), .out(multiplexer_2_out), .sel(comparator_2_lt));
  Multiplexer #(.select(4), .width(32)) multiplexer_3 (
    .in0(adder_1_out), .in1(subtractor_1_out), .in2(and_1_out), .in3(or_1_out), .in4(xor_1_out),
    .in5(multiplexer_1_out), .in6(multiplexer_2_out), .in7(shifter_1_out), .in8(shifter_2_out),
    .in9(shifter_3_out), .in10({32{1'b0}}), .in11({32{1'b0}}), .in12({32{1'b0}}), .in13({32{1'b0}}),
    .in14({32{1'b0}}), .in15({32{1'b0}}), .out(Result), .sel(ALUControl));

  // Notes on the sheet:
  //   ALUControl: initial=0x9
  //   B: initial=0x2
endmodule

module RegisterFile (
  input  [4:0] ReadReg1,
  input  [4:0] ReadReg2,
  input  [4:0] WriteReg,
  input  RegWrite,
  input  [31:0] WriteData,
  input  Clock,
  output [31:0] ReadData1,
  output [31:0] ReadData2
);

  wire WE1, WE2, WE3, WE4, WE5, WE6, WE7, WE8, WE9, WE10, WE11, WE12, WE13, WE14, WE15, WE16, WE17, WE18,
       WE19, WE20, WE21, WE22, WE23, WE24, WE25, WE26, WE27, WE28, WE29, WE30, WE31;
  wire [31:0] R1, R2, R3, R4, R5, R6, R7, R8, R9, R10, R11, R12, R13, R14, R15, R16, R17, R18, R19, R20, R21,
       R22, R23, R24, R25, R26, R27, R28, R29, R30, R31;

  Decoder #(.select(5)) decoder_1 (
    .out1(WE1), .out2(WE2), .out3(WE3), .out4(WE4), .out5(WE5), .out6(WE6), .out7(WE7), .out8(WE8),
    .out9(WE9), .out10(WE10), .out11(WE11), .out12(WE12), .out13(WE13), .out14(WE14), .out15(WE15),
    .out16(WE16), .out17(WE17), .out18(WE18), .out19(WE19), .out20(WE20), .out21(WE21), .out22(WE22),
    .out23(WE23), .out24(WE24), .out25(WE25), .out26(WE26), .out27(WE27), .out28(WE28), .out29(WE29),
    .out30(WE30), .out31(WE31), .sel(WriteReg), .en(RegWrite));  // open: out0
  Register #(.width(32)) register_1 (.D(WriteData), .en(WE1), .clk(Clock), .Q(R1));  // open: clr
  Register #(.width(32)) register_2 (.D(WriteData), .en(WE2), .clk(Clock), .Q(R2));  // open: clr
  Register #(.width(32)) register_3 (.D(WriteData), .en(WE3), .clk(Clock), .Q(R3));  // open: clr
  Register #(.width(32)) register_4 (.D(WriteData), .en(WE4), .clk(Clock), .Q(R4));  // open: clr
  Register #(.width(32)) register_5 (.D(WriteData), .en(WE5), .clk(Clock), .Q(R5));  // open: clr
  Register #(.width(32)) register_6 (.D(WriteData), .en(WE6), .clk(Clock), .Q(R6));  // open: clr
  Register #(.width(32)) register_7 (.D(WriteData), .en(WE7), .clk(Clock), .Q(R7));  // open: clr
  Register #(.width(32)) register_8 (.D(WriteData), .en(WE8), .clk(Clock), .Q(R8));  // open: clr
  Register #(.width(32)) register_9 (.D(WriteData), .en(WE9), .clk(Clock), .Q(R9));  // open: clr
  Register #(.width(32)) register_10 (.D(WriteData), .en(WE10), .clk(Clock), .Q(R10));  // open: clr
  Register #(.width(32)) register_11 (.D(WriteData), .en(WE11), .clk(Clock), .Q(R11));  // open: clr
  Register #(.width(32)) register_12 (.D(WriteData), .en(WE12), .clk(Clock), .Q(R12));  // open: clr
  Register #(.width(32)) register_13 (.D(WriteData), .en(WE13), .clk(Clock), .Q(R13));  // open: clr
  Register #(.width(32)) register_14 (.D(WriteData), .en(WE14), .clk(Clock), .Q(R14));  // open: clr
  Register #(.width(32)) register_15 (.D(WriteData), .en(WE15), .clk(Clock), .Q(R15));  // open: clr
  Register #(.width(32)) register_16 (.D(WriteData), .en(WE16), .clk(Clock), .Q(R16));  // open: clr
  Register #(.width(32)) register_17 (.D(WriteData), .en(WE17), .clk(Clock), .Q(R17));  // open: clr
  Register #(.width(32)) register_18 (.D(WriteData), .en(WE18), .clk(Clock), .Q(R18));  // open: clr
  Register #(.width(32)) register_19 (.D(WriteData), .en(WE19), .clk(Clock), .Q(R19));  // open: clr
  Register #(.width(32)) register_20 (.D(WriteData), .en(WE20), .clk(Clock), .Q(R20));  // open: clr
  Register #(.width(32)) register_21 (.D(WriteData), .en(WE21), .clk(Clock), .Q(R21));  // open: clr
  Register #(.width(32)) register_22 (.D(WriteData), .en(WE22), .clk(Clock), .Q(R22));  // open: clr
  Register #(.width(32)) register_23 (.D(WriteData), .en(WE23), .clk(Clock), .Q(R23));  // open: clr
  Register #(.width(32)) register_24 (.D(WriteData), .en(WE24), .clk(Clock), .Q(R24));  // open: clr
  Register #(.width(32)) register_25 (.D(WriteData), .en(WE25), .clk(Clock), .Q(R25));  // open: clr
  Register #(.width(32)) register_26 (.D(WriteData), .en(WE26), .clk(Clock), .Q(R26));  // open: clr
  Register #(.width(32)) register_27 (.D(WriteData), .en(WE27), .clk(Clock), .Q(R27));  // open: clr
  Register #(.width(32)) register_28 (.D(WriteData), .en(WE28), .clk(Clock), .Q(R28));  // open: clr
  Register #(.width(32)) register_29 (.D(WriteData), .en(WE29), .clk(Clock), .Q(R29));  // open: clr
  Register #(.width(32)) register_30 (.D(WriteData), .en(WE30), .clk(Clock), .Q(R30));  // open: clr
  Register #(.width(32)) register_31 (.D(WriteData), .en(WE31), .clk(Clock), .Q(R31));  // open: clr
  Multiplexer #(.select(5), .width(32)) multiplexer_1 (
    .in0({32{1'b0}}), .in1(R1), .in2(R2), .in3(R3), .in4(R4), .in5(R5), .in6(R6), .in7(R7), .in8(R8),
    .in9(R9), .in10(R10), .in11(R11), .in12(R12), .in13(R13), .in14(R14), .in15(R15), .in16(R16), .in17(R17),
    .in18(R18), .in19(R19), .in20(R20), .in21(R21), .in22(R22), .in23(R23), .in24(R24), .in25(R25),
    .in26(R26), .in27(R27), .in28(R28), .in29(R29), .in30(R30), .in31(R31), .out(ReadData1), .sel(ReadReg1));
  Multiplexer #(.select(5), .width(32)) multiplexer_2 (
    .in0({32{1'b0}}), .in1(R1), .in2(R2), .in3(R3), .in4(R4), .in5(R5), .in6(R6), .in7(R7), .in8(R8),
    .in9(R9), .in10(R10), .in11(R11), .in12(R12), .in13(R13), .in14(R14), .in15(R15), .in16(R16), .in17(R17),
    .in18(R18), .in19(R19), .in20(R20), .in21(R21), .in22(R22), .in23(R23), .in24(R24), .in25(R25),
    .in26(R26), .in27(R27), .in28(R28), .in29(R29), .in30(R30), .in31(R31), .out(ReadData2), .sel(ReadReg2));

  // Other names for the same wires on the sheet: OUT1[31:0] = ReadData1; OUT2[31:0] = ReadData2; SEL1[4:0] = ReadReg1;
  //   SEL2[4:0] = ReadReg2

  // Notes on the sheet:
  //   RegWrite: initial=0x1
  //   WriteData: initial=0x7b
  //   WriteReg: initial=0x1
endmodule

module ImmediateGenerator (
  input  [31:0] Instruction,
  input  [2:0] ImmType,
  output [31:0] Immediate,
  output [31:0] Imm_S,
  output [31:0] Imm_I,
  output [31:0] Imm_B,
  output [31:0] Imm_U,
  output [31:0] Imm_J
);

  assign Imm_I = {{20{Instruction[31]}}, Instruction[31:20]};  // Bit_Extender bit_extender_1
  Multiplexer #(.select(3), .width(32)) multiplexer_1 (
    .in0(Imm_I), .in1(Imm_S), .in2(Imm_B), .in3({Instruction[31:12], {12{1'b0}}}), .in4(Imm_J),
    .in5({32{1'b0}}), .in6({32{1'b0}}), .in7({32{1'b0}}), .out(Immediate), .sel(ImmType));
  assign Imm_S = {{20{Instruction[31]}}, {Instruction[31:25], Instruction[11:7]}};  // Bit_Extender bit_extender_2
  assign Imm_B = {{19{Instruction[31]}}, {Instruction[31], Instruction[7], Instruction[30:25], Instruction[11:8], 1'b0}};  // Bit_Extender bit_extender_3
  assign Imm_J = {{11{Instruction[31]}}, {Instruction[31], Instruction[19:12], Instruction[20], Instruction[30:21], 1'b0}};  // Bit_Extender bit_extender_4

  assign Imm_U = {Instruction[31:12], {12{1'b0}}};

  // Notes on the sheet:
  //   Instruction: initial=0xef
  //   ImmType: initial=0x4
endmodule

module ControlUnit (
  input  [6:0] Opcode,
  input  [2:0] Funct3,
  input  [6:0] Funct7,
  output [2:0] ImmType,
  output [3:0] ALUControl,
  output ALUSrc,
  output RegWrite,
  output MemRead,
  output MemWrite,
  output [1:0] ResultSrc,
  output Branch,
  output Jump,
  output BranchType
);

  wire ac0_a, ac0_b, ac0_c, ac1_a, ac2_a, ac2_b, add_addr, as_ab, f3_000, f3_001, f3_010, f3_011, f3_100,
       f3_101, f3_110, f3_111, f7_0, f7_20, I_f7_0, I_f7_20, isAUIPC, isBEQ, isBranchOpcode, isIType, isJALR,
       isLUI, isRType, isUImm, load_or_store, opADD, opADD_aux, opADD_I, opADD_R, opADD_RI, opAND, opAND_I,
       opAND_R, opOR, opOR_I, opOR_R, opSLL, opSLL_I, opSLL_R, opSLT, opSLT_I, opSLT_R, opSLTU, opSLTU_I,
       opSLTU_R, opSRA, opSRA_I, opSRA_R, opSRL, opSRL_I, opSRL_R, opSUB, opSUB_R, opXOR, opXOR_I, opXOR_R,
       R_f7_0, R_f7_20, rw_a, rw_a1, rw_ab;

  Comparator #(.width(7)) comparator_1 (.a(Opcode), .b(7'b0110011), .eq(isRType));  // open: gt, lt
  Comparator #(.width(7)) comparator_2 (.a(Opcode), .b(7'b0010011), .eq(isIType));  // open: gt, lt
  Comparator #(.width(7)) comparator_3 (.a(Opcode), .b(7'b0000011), .eq(MemRead));  // open: gt, lt
  Comparator #(.width(7)) comparator_4 (.a(Opcode), .b(7'b0100011), .eq(MemWrite));  // open: gt, lt
  Comparator #(.width(7)) comparator_5 (.a(Opcode), .b(7'b1100011), .eq(isBranchOpcode));  // open: gt, lt
  Comparator #(.width(7)) comparator_6 (.a(Opcode), .b(7'b0110111), .eq(isLUI));  // open: gt, lt
  Comparator #(.width(7)) comparator_7 (.a(Opcode), .b(7'b0010111), .eq(isAUIPC));  // open: gt, lt
  Comparator #(.width(7)) comparator_8 (.a(Opcode), .b(7'b1101111), .eq(ImmType[2]));  // open: gt, lt
  Comparator #(.width(7)) comparator_9 (.a(Opcode), .b(7'b1100111), .eq(isJALR));  // open: gt, lt
  Comparator #(.width(3)) comparator_10 (.a(Funct3), .b(3'b000), .eq(f3_000));  // open: gt, lt
  Comparator #(.width(3)) comparator_11 (.a(Funct3), .b(3'b001), .eq(f3_001));  // open: gt, lt
  Comparator #(.width(3)) comparator_12 (.a(Funct3), .b(3'b010), .eq(f3_010));  // open: gt, lt
  Comparator #(.width(3)) comparator_13 (.a(Funct3), .b(3'b011), .eq(f3_011));  // open: gt, lt
  Comparator #(.width(3)) comparator_14 (.a(Funct3), .b(3'b100), .eq(f3_100));  // open: gt, lt
  Comparator #(.width(3)) comparator_15 (.a(Funct3), .b(3'b101), .eq(f3_101));  // open: gt, lt
  Comparator #(.width(3)) comparator_16 (.a(Funct3), .b(3'b110), .eq(f3_110));  // open: gt, lt
  Comparator #(.width(3)) comparator_17 (.a(Funct3), .b(3'b111), .eq(f3_111));  // open: gt, lt
  Comparator #(.width(7)) comparator_18 (.a(Funct7), .b({7{1'b0}}), .eq(f7_0));  // open: gt, lt
  Comparator #(.width(7)) comparator_19 (.a(Funct7), .b(7'b0100000), .eq(f7_20));  // open: gt, lt
  and and_1 (R_f7_0, isRType, f7_0);
  and and_2 (R_f7_20, isRType, f7_20);
  and and_3 (I_f7_0, isIType, f7_0);
  and and_4 (I_f7_20, isIType, f7_20);
  and and_5 (opADD_R, R_f7_0, f3_000);
  and and_6 (opSUB_R, R_f7_20, f3_000);
  and and_7 (opAND_R, R_f7_0, f3_111);
  and and_8 (opOR_R, R_f7_0, f3_110);
  and and_9 (opXOR_R, R_f7_0, f3_100);
  and and_10 (opSLT_R, R_f7_0, f3_010);
  and and_11 (opSLTU_R, R_f7_0, f3_011);
  and and_12 (opSLL_R, R_f7_0, f3_001);
  and and_13 (opSRL_R, R_f7_0, f3_101);
  and and_14 (opSRA_R, R_f7_20, f3_101);
  and and_15 (opADD_I, isIType, f3_000);
  and and_16 (opAND_I, isIType, f3_111);
  and and_17 (opOR_I, isIType, f3_110);
  and and_18 (opXOR_I, isIType, f3_100);
  and and_19 (opSLT_I, isIType, f3_010);
  and and_20 (opSLTU_I, isIType, f3_011);
  and and_21 (opSLL_I, I_f7_0, f3_001);
  and and_22 (opSRL_I, I_f7_0, f3_101);
  and and_23 (opSRA_I, I_f7_20, f3_101);
  or or_1 (load_or_store, MemRead, MemWrite);
  or or_2 (add_addr, load_or_store, isJALR);
  or or_3 (isUImm, isLUI, isAUIPC);
  and and_24 (isBEQ, isBranchOpcode, f3_000);
  and and_25 (BranchType, isBranchOpcode, f3_001);
  or or_4 (Branch, isBEQ, BranchType);
  or or_5 (opADD_RI, opADD_R, opADD_I);
  or or_6 (opADD_aux, add_addr, isUImm);
  or or_7 (opADD, opADD_RI, opADD_aux);
  or or_8 (opSUB, opSUB_R, Branch);
  or or_9 (opAND, opAND_R, opAND_I);
  or or_10 (opOR, opOR_R, opOR_I);
  or or_11 (opXOR, opXOR_R, opXOR_I);
  or or_12 (opSLT, opSLT_R, opSLT_I);
  or or_13 (opSLTU, opSLTU_R, opSLTU_I);
  or or_14 (opSLL, opSLL_R, opSLL_I);
  or or_15 (opSRL, opSRL_R, opSRL_I);
  or or_16 (opSRA, opSRA_R, opSRA_I);
  or or_17 (ALUControl[3], opSRL, opSRA);
  or or_18 (ac2_a, opXOR, opSLT);
  or or_19 (ac2_b, opSLTU, opSLL);
  or or_20 (ALUControl[2], ac2_a, ac2_b);
  or or_21 (ac1_a, opAND, opOR);
  or or_22 (ALUControl[1], ac1_a, ac2_b);
  or or_23 (ac0_a, opSUB, opOR);
  or or_24 (ac0_b, opSLT, opSLL);
  or or_25 (ac0_c, ac0_a, ac0_b);
  or or_26 (ALUControl[0], ac0_c, opSRA);
  or or_27 (ImmType[1], isBranchOpcode, isUImm);
  or or_28 (ImmType[0], MemWrite, isUImm);
  or or_29 (rw_a1, isRType, isIType);
  or or_30 (rw_a, rw_a1, MemRead);
  or or_31 (Jump, ImmType[2], isJALR);
  or or_32 (rw_ab, rw_a, isUImm);
  or or_33 (RegWrite, rw_ab, Jump);
  or or_34 (as_ab, isIType, add_addr);
  or or_35 (ALUSrc, as_ab, isUImm);

  assign ResultSrc = {Jump, MemRead};

  // Other names for the same wires on the sheet: ALUCtrl0 = ALUControl[0]; ALUCtrl1 = ALUControl[1];
  //   ALUCtrl2 = ALUControl[2]; ALUCtrl3 = ALUControl[3]; isJAL = ImmType[2]; isBNE = BranchType; isStore = MemWrite;
  //   isLoad = MemRead; isJump = Jump; sig_ALUSrc = ALUSrc; sig_Branch = Branch; sig_RegWrite = RegWrite

  // Notes on the sheet:
  //   Opcode: initial=0x63
endmodule

module InstructionMemory (
  input  [31:0] Address,
  output [31:0] Instruction
);

  ROM #(.addrWidth(4), .dataWidth(32)) rom_1 (.addr(Address[5:2]), .data(Instruction));

  // Notes on the sheet:
  //   contents of rom_1 (hex, n*v repeats v):
  //   500093 700113 2081b3 302023 2203 100073 13 13
endmodule

module DataMemory (
  input  [31:0] Address,
  input  [31:0] WriteData,
  input  MemWrite,
  input  Clock,
  input  MemRead,
  output [31:0] ReadData
);

  wire [31:0] ram_1_dout;

  RAM #(.addrWidth(4), .asyncread("true"), .dataWidth(32)) ram_1 (
    .addr(Address[5:2]), .we(MemWrite), .oe(1'b1), .clk(Clock), .din(WriteData), .dout(ram_1_dout));
  Multiplexer #(.width(32)) multiplexer_1 (.in0({32{1'b0}}), .in1(ram_1_dout), .out(ReadData), .sel(MemRead));
endmodule

module PC (
  input  [31:0] PCNext,
  input  Reset,
  input  Clock,
  output [31:0] PCOut
);

  wire [31:0] multiplexer_1_out;

  Multiplexer #(.width(32)) multiplexer_1 (.in0(PCNext), .in1({32{1'b0}}), .out(multiplexer_1_out), .sel(Reset));
  Register #(.width(32)) register_1 (.D(multiplexer_1_out), .clk(Clock), .Q(PCOut));  // open: en, clr

  // Notes on the sheet:
  //   Clock: initial=0x8
endmodule

module SingleCycleCPU (
  input  Clock,
  input  Reset,
  output [31:0] DebugPC,
  output [31:0] DebugInstruction,
  output [31:0] DebugALUResult
);

  wire ALUSrc, beq_cond, bne_cond, Branch, branch_cond, BranchTaken, BranchType, Equal, isAUIPC, isBEQ_type,
       isJAL, isJALR, isLUI, Jump, MemRead, MemWrite, NotEqual, RegWrite, selJAL, selJALR;
  wire [1:0] ResultSrc;
  wire [2:0] ImmType;
  wire [3:0] ALUControl;
  wire [31:0] adder_3_out, ALUA, ALUB, Imm32, MemReadData, multiplexer_1_out, multiplexer_3_out,
       multiplexer_4_out, multiplexer_7_out, PCImmTarget, PCJALR, PCNext, PCPlus4, RegA, RegB, WriteBackData;

  Comparator #(.width(7)) comparator_1 (.a(DebugInstruction[6:0]), .b(7'b0110111), .eq(isLUI));  // open: gt, lt
  Comparator #(.width(7)) comparator_2 (.a(DebugInstruction[6:0]), .b(7'b0010111), .eq(isAUIPC));  // open: gt, lt
  Comparator #(.width(7)) comparator_3 (.a(DebugInstruction[6:0]), .b(7'b1101111), .eq(isJAL));  // open: gt, lt
  Comparator #(.width(7)) comparator_4 (.a(DebugInstruction[6:0]), .b(7'b1100111), .eq(isJALR));  // open: gt, lt
  PC pc_1 (.PCNext(PCNext), .Reset(Reset), .Clock(Clock), .PCOut(DebugPC));
  Multiplexer #(.width(32)) multiplexer_1 (.in0(PCPlus4), .in1(PCImmTarget), .out(multiplexer_1_out), .sel(selJAL));
  InstructionMemory instructionmemory_1 (.Address(DebugPC), .Instruction(DebugInstruction));
  ControlUnit controlunit_1 (
    .Opcode(DebugInstruction[6:0]), .Funct3(DebugInstruction[14:12]), .Funct7(DebugInstruction[31:25]),
    .ImmType(ImmType), .ALUControl(ALUControl), .ALUSrc(ALUSrc), .RegWrite(RegWrite), .MemRead(MemRead),
    .MemWrite(MemWrite), .ResultSrc(ResultSrc), .Branch(Branch), .Jump(Jump), .BranchType(BranchType));
  ImmediateGenerator immediategenerator_1 (
    .Instruction(DebugInstruction), .ImmType(ImmType), .Immediate(Imm32));  // open: Imm_S, Imm_I, Imm_B, Imm_U, Imm_J
  Multiplexer #(.width(32)) multiplexer_2 (.in0(RegB), .in1(Imm32), .out(ALUB), .sel(ALUSrc));
  Multiplexer #(.width(32)) multiplexer_3 (.in0(RegA), .in1(DebugPC), .out(multiplexer_3_out), .sel(isAUIPC));
  Multiplexer #(.width(32)) multiplexer_4 (
    .in0(DebugALUResult), .in1(MemReadData), .out(multiplexer_4_out), .sel(ResultSrc[0]));
  Multiplexer #(.width(32)) multiplexer_5 (.in0(multiplexer_3_out), .in1({32{1'b0}}), .out(ALUA), .sel(isLUI));
  Multiplexer #(.width(32)) multiplexer_6 (
    .in0(multiplexer_4_out), .in1(PCPlus4), .out(WriteBackData), .sel(ResultSrc[1]));
  Multiplexer #(.width(32)) multiplexer_7 (
    .in0(multiplexer_1_out), .in1(PCJALR), .out(multiplexer_7_out), .sel(selJALR));
  Multiplexer #(.width(32)) multiplexer_8 (.in0(multiplexer_7_out), .in1(PCImmTarget), .out(PCNext), .sel(BranchTaken));
  Adder #(.width(32)) adder_1 (.a(DebugPC), .b(32'h4), .out(PCPlus4), .cin(1'b0));  // open: cout
  Adder #(.width(32)) adder_2 (.a(DebugPC), .b(Imm32), .out(PCImmTarget), .cin(1'b0));  // open: cout
  Adder #(.width(32)) adder_3 (.a(RegA), .b(Imm32), .out(adder_3_out), .cin(1'b0));  // open: cout
  Comparator #(.width(32)) comparator_5 (.a(RegA), .b(RegB), .eq(Equal));  // open: gt, lt
  Comparator #(.width(1)) comparator_6 (.a(BranchType), .b(1'b0), .eq(isBEQ_type));  // open: gt, lt
  Comparator #(.width(1)) comparator_7 (.a(Equal), .b(1'b0), .eq(NotEqual));  // open: gt, lt
  assign PCJALR = adder_3_out & 32'hfffffffe;  // AND_Gate and_1, 32 bits wide
  RegisterFile registerfile_1 (
    .ReadReg1(DebugInstruction[19:15]), .ReadReg2(DebugInstruction[24:20]),
    .WriteReg(DebugInstruction[11:7]), .RegWrite(RegWrite), .WriteData(WriteBackData), .Clock(Clock),
    .ReadData1(RegA), .ReadData2(RegB));
  and and_2 (beq_cond, isBEQ_type, Equal);
  and and_3 (bne_cond, BranchType, NotEqual);
  or or_1 (branch_cond, beq_cond, bne_cond);
  and and_4 (BranchTaken, Branch, branch_cond);
  and and_5 (selJAL, Jump, isJAL);
  and and_6 (selJALR, Jump, isJALR);
  ALU alu_1 (.A(ALUA), .B(ALUB), .ALUControl(ALUControl), .Result(DebugALUResult));
  DataMemory datamemory_1 (
    .Address(DebugALUResult), .WriteData(RegB), .MemWrite(MemWrite), .Clock(Clock), .MemRead(MemRead),
    .ReadData(MemReadData));

  // Other names for the same wires on the sheet: ALUResult[31:0] = DebugALUResult;
  //   Instruction[31:0] = DebugInstruction; Opcode[6:0] = DebugInstruction[6:0]; rd[4:0] = DebugInstruction[11:7];
  //   funct3[2:0] = DebugInstruction[14:12]; rs1[4:0] = DebugInstruction[19:15]; rs2[4:0] = DebugInstruction[24:20];
  //   funct7[6:0] = DebugInstruction[31:25]; PCOut[31:0] = DebugPC
endmodule
